# Fritzing sketch chef_station_chopping_module_editable (saved by Fritzing 1.0.7)
breadboards: 1

parts:
  Waveshare_ESP32-P4-ETH_/_ESP32-P4-POE-ETH = chef_chop_waveshare_esp32_poe_eth
  5V_AUX_input_from_master_power_rails = chef_chop_external_5v_supply
  5V_AUX_local_accessory_rail = chef_chop_local_5v_aux_rail
  ESP32_3_3V_sensor_rail = chef_chop_esp32_3v3_sensor_rail
  COMMON_GND_local_reference_rail = chef_chop_common_ground_rail
  R1_piezo_AO_1k-10k_series_resistor = chef_chop_resistor_piezo_series [Resistance=1k-10k]
  Optional_bidirectional_I2C_level_shifter = chef_chop_i2c_level_shifter
  20x4_I2C_LCD_above_cutting_board = chef_chop_i2c_lcd
  Piezo_knock/vibration_sensor_module = chef_chop_piezo_module
  wp_0_0_19 = chef_chop_waypoint
  wp_1_1_20 = chef_chop_waypoint
  wp_3_0_21 = chef_chop_waypoint
  wp_4_1_22 = chef_chop_waypoint
  wp_6_0_23 = chef_chop_waypoint
  wp_7_1_24 = chef_chop_waypoint
  wp_9_0_25 = chef_chop_waypoint
  wp_10_1_26 = chef_chop_waypoint
  wp_12_0_27 = chef_chop_waypoint
  wp_13_1_28 = chef_chop_waypoint
  wp_15_0_29 = chef_chop_waypoint
  wp_16_1_30 = chef_chop_waypoint
  wp_18_0_31 = chef_chop_waypoint
  wp_19_1_32 = chef_chop_waypoint
  wp_21_0_33 = chef_chop_waypoint
  wp_22_1_34 = chef_chop_waypoint
  wp_24_0_35 = chef_chop_waypoint
  wp_25_1_36 = chef_chop_waypoint
  wp_27_0_37 = chef_chop_waypoint
  wp_28_1_38 = chef_chop_waypoint
  wp_30_0_39 = chef_chop_waypoint
  wp_31_1_40 = chef_chop_waypoint
  wp_33_0_41 = chef_chop_waypoint
  wp_34_1_42 = chef_chop_waypoint
  wp_36_0_43 = chef_chop_waypoint
  wp_37_1_44 = chef_chop_waypoint
  wp_39_0_45 = chef_chop_waypoint
  wp_40_1_46 = chef_chop_waypoint
  wp_42_0_47 = chef_chop_waypoint
  wp_43_1_48 = chef_chop_waypoint
  wp_45_0_49 = chef_chop_waypoint
  wp_46_1_50 = chef_chop_waypoint
  wp_48_0_51 = chef_chop_waypoint
  wp_49_1_52 = chef_chop_waypoint
  wp_51_0_53 = chef_chop_waypoint
  wp_52_1_54 = chef_chop_waypoint

nets:
  N1: Waveshare_ESP32-P4-ETH_/_ESP32-P4-POE-ETH.connector0, ESP32_3_3V_sensor_rail.tap0, wp_6_0_23.pin, wp_7_1_24.pin
  N2: Waveshare_ESP32-P4-ETH_/_ESP32-P4-POE-ETH.connector1, COMMON_GND_local_reference_rail.tap0, wp_9_0_25.pin, wp_10_1_26.pin
  N3: Waveshare_ESP32-P4-ETH_/_ESP32-P4-POE-ETH.connector10, Optional_bidirectional_I2C_level_shifter.lv_sda, wp_42_0_47.pin, wp_43_1_48.pin
  N4: Waveshare_ESP32-P4-ETH_/_ESP32-P4-POE-ETH.connector13, Optional_bidirectional_I2C_level_shifter.lv_scl, wp_45_0_49.pin, wp_46_1_50.pin
  N5: Waveshare_ESP32-P4-ETH_/_ESP32-P4-POE-ETH.connector18, R1_piezo_AO_1k-10k_series_resistor.connector0, wp_21_0_33.pin, wp_22_1_34.pin
  N6: 5V_AUX_input_from_master_power_rails.gnd, COMMON_GND_local_reference_rail.tap11, wp_3_0_21.pin, wp_4_1_22.pin
  N7: 5V_AUX_input_from_master_power_rails.vcc, 5V_AUX_local_accessory_rail.tap11, wp_0_0_19.pin, wp_1_1_20.pin
  N8: 5V_AUX_local_accessory_rail.tap12, Optional_bidirectional_I2C_level_shifter.hv, wp_33_0_41.pin, wp_34_1_42.pin
  N9: 5V_AUX_local_accessory_rail.tap15, 20x4_I2C_LCD_above_cutting_board.vcc, wp_24_0_35.pin, wp_25_1_36.pin
  N10: ESP32_3_3V_sensor_rail.tap10, Optional_bidirectional_I2C_level_shifter.lv, wp_30_0_39.pin, wp_31_1_40.pin
  N11: ESP32_3_3V_sensor_rail.tap16, Piezo_knock/vibration_sensor_module.vcc, wp_12_0_27.pin, wp_13_1_28.pin
  N12: COMMON_GND_local_reference_rail.tap10, Optional_bidirectional_I2C_level_shifter.gnd_l, wp_36_0_43.pin, wp_37_1_44.pin
  N13: COMMON_GND_local_reference_rail.tap12, Optional_bidirectional_I2C_level_shifter.gnd_h, wp_39_0_45.pin, wp_40_1_46.pin
  N14: COMMON_GND_local_reference_rail.tap15, 20x4_I2C_LCD_above_cutting_board.gnd, wp_27_0_37.pin, wp_28_1_38.pin
  N15: COMMON_GND_local_reference_rail.tap16, Piezo_knock/vibration_sensor_module.gnd, wp_15_0_29.pin, wp_16_1_30.pin
  N16: R1_piezo_AO_1k-10k_series_resistor.connector1, Piezo_knock/vibration_sensor_module.ao, wp_18_0_31.pin, wp_19_1_32.pin
  N17: Optional_bidirectional_I2C_level_shifter.hv_scl, 20x4_I2C_LCD_above_cutting_board.scl, wp_51_0_53.pin, wp_52_1_54.pin
  N18: Optional_bidirectional_I2C_level_shifter.hv_sda, 20x4_I2C_LCD_above_cutting_board.sda, wp_48_0_51.pin, wp_49_1_52.pin
