# Fritzing sketch chef_station_chopping_module_editable (saved by Fritzing 1.0.3)

parts:
  Chef_Station_"Chopping_Module"_wiring = Chef Station "Chopping Module" wiring  # not connected
  Pin_assignment_summary = Pin assignment summary  # not connected
  Power_and_common_ground = Power and common ground  # not connected
  Piezo_protection_and_thresholding = Piezo protection and thresholding  # not connected
  Chop_debounce = Chop debounce  # not connected
  LCD_I2C_notes = LCD I2C notes  # not connected
  No_hardware_sync_terminals = No hardware sync terminals  # not connected
  Firmware_behavior = Firmware behavior  # not connected
  Waveshare_ESP32-P4-ETH_/_ESP32-P4-POE-ETH = Waveshare ESP32-P4-ETH / ESP32-P4-POE-ETH
  5V_AUX_input_from_master_power_rails = 5V_AUX rail input from master power distribution
  5V_AUX_local_accessory_rail = 5V_AUX rail
  ESP32_3_3V_sensor_rail = ESP32 3.3V rail
  COMMON_GND_local_reference_rail = COMMON_GND rail
  R1_piezo_AO_1k-10k_series_resistor = 1k-10k piezo AO series resistor [Resistance=1k-10k]
  Optional_bidirectional_I2C_level_shifter = Optional bidirectional I2C level shifter
  20x4_I2C_LCD_above_cutting_board = 20x4 I2C character LCD
  Piezo_knock/vibration_sensor_module = Piezo knock/vibration sensor module
  Cutting_board_physical_layout_with_protected_piezo = Cutting board physical layout  # not connected
  Raw_piezo_disc_alternative_protection_circuit = Raw piezo input protection alternative  # not connected
  wp_0_0_19 = Wire waypoint
  wp_1_1_20 = Wire waypoint
  wp_3_0_21 = Wire waypoint
  wp_4_1_22 = Wire waypoint
  wp_6_0_23 = Wire waypoint
  wp_7_1_24 = Wire waypoint
  wp_9_0_25 = Wire waypoint
  wp_10_1_26 = Wire waypoint
  wp_12_0_27 = Wire waypoint
  wp_13_1_28 = Wire waypoint
  wp_15_0_29 = Wire waypoint
  wp_16_1_30 = Wire waypoint
  wp_18_0_31 = Wire waypoint
  wp_19_1_32 = Wire waypoint
  wp_21_0_33 = Wire waypoint
  wp_22_1_34 = Wire waypoint
  wp_24_0_35 = Wire waypoint
  wp_25_1_36 = Wire waypoint
  wp_27_0_37 = Wire waypoint
  wp_28_1_38 = Wire waypoint
  wp_30_0_39 = Wire waypoint
  wp_31_1_40 = Wire waypoint
  wp_33_0_41 = Wire waypoint
  wp_34_1_42 = Wire waypoint
  wp_36_0_43 = Wire waypoint
  wp_37_1_44 = Wire waypoint
  wp_39_0_45 = Wire waypoint
  wp_40_1_46 = Wire waypoint
  wp_42_0_47 = Wire waypoint
  wp_43_1_48 = Wire waypoint
  wp_45_0_49 = Wire waypoint
  wp_46_1_50 = Wire waypoint
  wp_48_0_51 = Wire waypoint
  wp_49_1_52 = Wire waypoint
  wp_51_0_53 = Wire waypoint
  wp_52_1_54 = Wire waypoint
  Manhattan_breadboard_and_rails_area = Breadboard and power rails area  # not connected

nets:
  N1: Waveshare_ESP32-P4-ETH_/_ESP32-P4-POE-ETH.3V3_sensor_rail, ESP32_3_3V_sensor_rail.ESP32_3.3V_rail_tap_0, ESP32_3_3V_sensor_rail.ESP32_3.3V_rail_tap_10, ESP32_3_3V_sensor_rail.ESP32_3.3V_rail_tap_16, Optional_bidirectional_I2C_level_shifter.LV_3.3V, Piezo_knock/vibration_sensor_module.VCC_3.3V, wp_6_0_23.waypoint, wp_7_1_24.waypoint, wp_12_0_27.waypoint, wp_13_1_28.waypoint, wp_30_0_39.waypoint, wp_31_1_40.waypoint
  GND: Waveshare_ESP32-P4-ETH_/_ESP32-P4-POE-ETH.GND, 5V_AUX_input_from_master_power_rails.COMMON_GND, COMMON_GND_local_reference_rail.COMMON_GND_rail_tap_0, COMMON_GND_local_reference_rail.COMMON_GND_rail_tap_10, COMMON_GND_local_reference_rail.COMMON_GND_rail_tap_11, COMMON_GND_local_reference_rail.COMMON_GND_rail_tap_12, COMMON_GND_local_reference_rail.COMMON_GND_rail_tap_15, COMMON_GND_local_reference_rail.COMMON_GND_rail_tap_16, Optional_bidirectional_I2C_level_shifter.GND, 20x4_I2C_LCD_above_cutting_board.LCD_GND, Piezo_knock/vibration_sensor_module.GND, wp_3_0_21.waypoint, wp_4_1_22.waypoint, wp_9_0_25.waypoint, wp_10_1_26.waypoint, wp_15_0_29.waypoint, wp_16_1_30.waypoint, wp_27_0_37.waypoint, wp_28_1_38.waypoint, wp_36_0_43.waypoint, wp_37_1_44.waypoint, wp_39_0_45.waypoint, wp_40_1_46.waypoint
  N2: Waveshare_ESP32-P4-ETH_/_ESP32-P4-POE-ETH.SDA/GPIO7, Optional_bidirectional_I2C_level_shifter.LV1_SDA_from_ESP32_SDA/GPIO7, wp_42_0_47.waypoint, wp_43_1_48.waypoint
  N3: Waveshare_ESP32-P4-ETH_/_ESP32-P4-POE-ETH.SCL/GPIO8, Optional_bidirectional_I2C_level_shifter.LV2_SCL_from_ESP32_SCL/GPIO8, wp_45_0_49.waypoint, wp_46_1_50.waypoint
  N4: Waveshare_ESP32-P4-ETH_/_ESP32-P4-POE-ETH.GPIO16_/_ADC1_CH0, R1_piezo_AO_1k-10k_series_resistor.lead_A, wp_21_0_33.waypoint, wp_22_1_34.waypoint
  N5: 5V_AUX_input_from_master_power_rails.5V_AUX, 5V_AUX_local_accessory_rail.5V_AUX_rail_tap_11, 5V_AUX_local_accessory_rail.5V_AUX_rail_tap_12, 5V_AUX_local_accessory_rail.5V_AUX_rail_tap_15, Optional_bidirectional_I2C_level_shifter.HV_5V, 20x4_I2C_LCD_above_cutting_board.LCD_VCC_5V_or_confirmed_3.3V, wp_0_0_19.waypoint, wp_1_1_20.waypoint, wp_24_0_35.waypoint, wp_25_1_36.waypoint, wp_33_0_41.waypoint, wp_34_1_42.waypoint
  N6: R1_piezo_AO_1k-10k_series_resistor.lead_B, Piezo_knock/vibration_sensor_module.AO_analog_output, wp_18_0_31.waypoint, wp_19_1_32.waypoint
  N7: Optional_bidirectional_I2C_level_shifter.HV2_SCL_to_LCD, 20x4_I2C_LCD_above_cutting_board.LCD_SCL, wp_51_0_53.waypoint, wp_52_1_54.waypoint
  N8: Optional_bidirectional_I2C_level_shifter.HV1_SDA_to_LCD, 20x4_I2C_LCD_above_cutting_board.LCD_SDA, wp_48_0_51.waypoint, wp_49_1_52.waypoint
