# Fritzing sketch chef_station_garnish_placement_editable (saved by Fritzing 1.0.3)

parts:
  Chef_Station_"Garnish_Placement"_ESP32_Wiring = Chef Station "Garnish Placement" ESP32 Wiring  # not connected
  Pin_assignment_summary = Pin assignment summary  # not connected
  Capacitive_electrode_notes = Capacitive electrode notes  # not connected
  Power_and_logic_notes = Power and logic notes  # not connected
  Firmware_behavior = Firmware behavior  # not connected
  DONE_logic = DONE logic  # not connected
  Waveshare_ESP32-P4-POE-ETH_/_ESP32-P4-POE-ETH-NH = Waveshare ESP32-P4-POE-ETH / ESP32-P4-POE-ETH-NH
  Waveshare_ESP32-P4_PoE_module = Waveshare ESP32-P4 PoE module  # not connected
  5V_LED_input_from_master_power_rails = Named 5V accessory rail input
  5V_AUDIO_SERVO_input_from_master_power_rails = Named 5V accessory rail input
  5V_LED_local_rail = 5V_LED rail
  5V_AUDIO_SERVO_local_rail = 5V_AUDIO_SERVO rail
  COMMON_GND_rail = COMMON_GND rail
  R4_330_ohm_LED_data_resistor_(330-470_ohm_OK) = 330-470 ohm LED data resistor [Resistance="330 ohm"]
  R1_1k_CENTER_electrode_series_resistor = 1k series resistor [Resistance=1k]
  R2_1k_INNER_electrode_series_resistor = 1k series resistor [Resistance=1k]
  R3_1k_OUTER_electrode_series_resistor = 1k series resistor [Resistance=1k]
  Series_resistors = Series resistors  # not connected
  3-contact_addressable_RGB_strip_+5V_/_DIN_/_GND = 3-contact addressable RGB strip: +5V / DIN / GND
  C1_1000uF_electrolytic_near_LED_strip = Electrolytic Capacitor [Capacitance=1000uF package=THT]
  RGB_strip = RGB strip  # not connected
  Fake_steak_bullseye_capacitive_target = Fake steak bullseye capacitive electrodes
  Small_hobby_servo_timer_pointer = Small hobby servo timer pointer
  C2_470uF-1000uF_electrolytic_near_servo = Electrolytic Capacitor [Capacitance=470uF-1000uF package=THT]
  Servo_timer = Servo timer  # not connected
  DONE_momentary_pushbutton = DONE momentary pushbutton
  Breadboard_and_power_rails_area = Breadboard / power rails area  # not connected
  wp_0_1_27 = Wire waypoint
  wp_2_0_28 = Wire waypoint
  wp_3_1_29 = Wire waypoint
  wp_5_0_30 = Wire waypoint
  wp_6_1_31 = Wire waypoint
  wp_8_0_32 = Wire waypoint
  wp_9_1_33 = Wire waypoint
  wp_11_0_34 = Wire waypoint
  wp_12_1_35 = Wire waypoint
  wp_14_0_36 = Wire waypoint
  wp_15_1_37 = Wire waypoint
  wp_17_0_38 = Wire waypoint
  wp_18_1_39 = Wire waypoint
  wp_20_0_40 = Wire waypoint
  wp_21_1_41 = Wire waypoint
  wp_23_0_42 = Wire waypoint
  wp_24_1_43 = Wire waypoint
  wp_26_1_44 = Wire waypoint
  wp_28_1_45 = Wire waypoint
  wp_30_0_46 = Wire waypoint
  wp_31_1_47 = Wire waypoint
  wp_33_0_48 = Wire waypoint
  wp_34_1_49 = Wire waypoint
  wp_36_0_50 = Wire waypoint
  wp_37_1_51 = Wire waypoint
  wp_39_0_52 = Wire waypoint
  wp_40_1_53 = Wire waypoint
  wp_42_0_54 = Wire waypoint
  wp_43_1_55 = Wire waypoint
  wp_45_0_56 = Wire waypoint
  wp_46_1_57 = Wire waypoint
  wp_48_0_58 = Wire waypoint
  wp_49_1_59 = Wire waypoint
  wp_51_0_60 = Wire waypoint
  wp_52_1_61 = Wire waypoint
  wp_54_0_62 = Wire waypoint
  wp_55_1_63 = Wire waypoint
  wp_57_0_64 = Wire waypoint
  wp_58_1_65 = Wire waypoint
  wp_60_0_66 = Wire waypoint
  wp_61_1_67 = Wire waypoint
  wp_63_0_68 = Wire waypoint
  wp_64_1_69 = Wire waypoint
  wp_66_0_70 = Wire waypoint
  wp_67_1_71 = Wire waypoint

nets:
  GND: Waveshare_ESP32-P4-POE-ETH_/_ESP32-P4-POE-ETH-NH.GND, 5V_LED_input_from_master_power_rails.COMMON_GND, 5V_AUDIO_SERVO_input_from_master_power_rails.COMMON_GND, COMMON_GND_rail.COMMON_GND_rail_tap_0, COMMON_GND_rail.COMMON_GND_rail_tap_1, COMMON_GND_rail.COMMON_GND_rail_tap_2, COMMON_GND_rail.COMMON_GND_rail_tap_7, COMMON_GND_rail.COMMON_GND_rail_tap_13, COMMON_GND_rail.COMMON_GND_rail_tap_15, 3-contact_addressable_RGB_strip_+5V_/_DIN_/_GND.GND, C1_1000uF_electrolytic_near_LED_strip.-, Small_hobby_servo_timer_pointer.GND_brown/black_wire, C2_470uF-1000uF_electrolytic_near_servo.-, DONE_momentary_pushbutton.DONE_GND, wp_2_0_28.waypoint, wp_3_1_29.waypoint, wp_8_0_32.waypoint, wp_9_1_33.waypoint, wp_11_0_34.waypoint, wp_12_1_35.waypoint, wp_17_0_38.waypoint, wp_18_1_39.waypoint, wp_23_0_42.waypoint, wp_24_1_43.waypoint, wp_28_1_45.waypoint, wp_33_0_48.waypoint, wp_34_1_49.waypoint, wp_36_0_50.waypoint, wp_37_1_51.waypoint
  N1: Waveshare_ESP32-P4-POE-ETH_/_ESP32-P4-POE-ETH-NH.GPIO23_/_LED_DATA, R4_330_ohm_LED_data_resistor_(330-470_ohm_OK).lead_A, wp_39_0_52.waypoint, wp_40_1_53.waypoint
  N2: Waveshare_ESP32-P4-POE-ETH_/_ESP32-P4-POE-ETH-NH.GPIO2_/_CENTER, R1_1k_CENTER_electrode_series_resistor.lead_A, wp_51_0_60.waypoint, wp_52_1_61.waypoint
  N3: Waveshare_ESP32-P4-POE-ETH_/_ESP32-P4-POE-ETH-NH.GPIO3_/_INNER, R2_1k_INNER_electrode_series_resistor.lead_A, wp_54_0_62.waypoint, wp_55_1_63.waypoint
  N4: Waveshare_ESP32-P4-POE-ETH_/_ESP32-P4-POE-ETH-NH.GPIO32_/_SERVO_SIG, Small_hobby_servo_timer_pointer.signal, wp_45_0_56.waypoint, wp_46_1_57.waypoint
  N5: Waveshare_ESP32-P4-POE-ETH_/_ESP32-P4-POE-ETH-NH.GPIO26_/_DONE, DONE_momentary_pushbutton.DONE_signal_to_GPIO26, wp_48_0_58.waypoint, wp_49_1_59.waypoint
  N6: Waveshare_ESP32-P4-POE-ETH_/_ESP32-P4-POE-ETH-NH.GPIO6_/_OUTER, R3_1k_OUTER_electrode_series_resistor.lead_A, wp_57_0_64.waypoint, wp_58_1_65.waypoint
  N7: 5V_LED_input_from_master_power_rails.+5V_rail_input, 5V_LED_local_rail.5V_LED_rail_tap_0, 5V_LED_local_rail.5V_LED_rail_tap_13, 3-contact_addressable_RGB_strip_+5V_/_DIN_/_GND.+5V, C1_1000uF_electrolytic_near_LED_strip.+, wp_0_1_27.waypoint, wp_14_0_36.waypoint, wp_15_1_37.waypoint, wp_20_0_40.waypoint, wp_21_1_41.waypoint
  N8: 5V_AUDIO_SERVO_input_from_master_power_rails.+5V_rail_input, 5V_AUDIO_SERVO_local_rail.5V_AUDIO_SERVO_rail_tap_0, 5V_AUDIO_SERVO_local_rail.5V_AUDIO_SERVO_rail_tap_15, Small_hobby_servo_timer_pointer.+5V_red_wire, C2_470uF-1000uF_electrolytic_near_servo.+, wp_5_0_30.waypoint, wp_6_1_31.waypoint, wp_26_1_44.waypoint, wp_30_0_46.waypoint, wp_31_1_47.waypoint
  N9: R4_330_ohm_LED_data_resistor_(330-470_ohm_OK).lead_B, 3-contact_addressable_RGB_strip_+5V_/_DIN_/_GND.DIN, wp_42_0_54.waypoint, wp_43_1_55.waypoint
  N10: R1_1k_CENTER_electrode_series_resistor.lead_B, Fake_steak_bullseye_capacitive_target.CENTER_/_PERFECT_electrode, wp_60_0_66.waypoint, wp_61_1_67.waypoint
  N11: R2_1k_INNER_electrode_series_resistor.lead_B, Fake_steak_bullseye_capacitive_target.INNER_/_GOOD_electrode, wp_63_0_68.waypoint, wp_64_1_69.waypoint
  N12: R3_1k_OUTER_electrode_series_resistor.lead_B, Fake_steak_bullseye_capacitive_target.OUTER_/_OK_electrode, wp_66_0_70.waypoint, wp_67_1_71.waypoint
