# Fritzing sketch chef_station_simon_lane_routed_editable (saved by Fritzing 1.0.7)

parts:
  DOIT_ESP32_DevKit_V1 = esp32_p30_w11 [part_number=ESP32S-PIN30]
  +12V_LED_rail = chef_simon_vplus_12v_rail
  Common_GND_rail = chef_simon_common_ground_rail
  wp_0_0_5 = chef_simon_wire_waypoint
  wp_1_1_6 = chef_simon_wire_waypoint
  wp_2_2_7 = chef_simon_wire_waypoint
  R1_1k_gate = 1k Ω Resistor [Resistance=1k package=THT]
  R1_10k_gate_pulldown = 10k Ω Resistor [Resistance=10k package=THT]
  Q1_IRFB11N50APBF = Basic FET N-Channel [package="TO220 [THT]"]
  BTN1_4-terminal_plug = Camdenboss CTB0158-4 [part_number=CTB0158-4 package=THT]
  Ingredient_1_arcade_button_visual = Arcade Button (red)
  BTN1_local_GND_bus = chef_simon_local_ground_bus
  wp_4_0_17 = chef_simon_wire_waypoint
  wp_5_1_18 = chef_simon_wire_waypoint
  wp_6_2_19 = chef_simon_wire_waypoint
  wp_8_0_20 = chef_simon_wire_waypoint
  wp_9_1_21 = chef_simon_wire_waypoint
  wp_10_2_22 = chef_simon_wire_waypoint
  wp_12_0_23 = chef_simon_wire_waypoint
  wp_14_0_24 = chef_simon_wire_waypoint
  wp_16_0_25 = chef_simon_wire_waypoint
  wp_17_1_26 = chef_simon_wire_waypoint
  wp_18_2_27 = chef_simon_wire_waypoint
  wp_20_0_28 = chef_simon_wire_waypoint
  wp_21_1_29 = chef_simon_wire_waypoint
  wp_22_2_30 = chef_simon_wire_waypoint
  wp_24_0_31 = chef_simon_wire_waypoint
  wp_25_1_32 = chef_simon_wire_waypoint
  wp_26_2_33 = chef_simon_wire_waypoint
  wp_28_0_34 = chef_simon_wire_waypoint
  wp_29_1_35 = chef_simon_wire_waypoint
  wp_30_2_36 = chef_simon_wire_waypoint
  wp_32_0_37 = chef_simon_wire_waypoint
  wp_34_0_38 = chef_simon_wire_waypoint
  wp_36_0_39 = chef_simon_wire_waypoint
  wp_37_1_40 = chef_simon_wire_waypoint
  wp_38_2_41 = chef_simon_wire_waypoint
  wp_40_0_42 = chef_simon_wire_waypoint
  wp_41_1_43 = chef_simon_wire_waypoint
  wp_42_2_44 = chef_simon_wire_waypoint
  R2_1k_gate = 1k Ω Resistor [Resistance=1k package=THT]
  R2_10k_gate_pulldown = 10k Ω Resistor [Resistance=10k package=THT]
  Q2_IRFB11N50APBF = Basic FET N-Channel [package="TO220 [THT]"]
  BTN2_4-terminal_plug = Camdenboss CTB0158-4 [part_number=CTB0158-4 package=THT]
  Ingredient_2_arcade_button_visual = chef_simon_library_derived_green_arcade_button
  BTN2_local_GND_bus = chef_simon_local_ground_bus
  wp_44_0_54 = chef_simon_wire_waypoint
  wp_45_1_55 = chef_simon_wire_waypoint
  wp_46_2_56 = chef_simon_wire_waypoint
  wp_48_0_57 = chef_simon_wire_waypoint
  wp_49_1_58 = chef_simon_wire_waypoint
  wp_50_2_59 = chef_simon_wire_waypoint
  wp_52_0_60 = chef_simon_wire_waypoint
  wp_54_0_61 = chef_simon_wire_waypoint
  wp_56_0_62 = chef_simon_wire_waypoint
  wp_57_1_63 = chef_simon_wire_waypoint
  wp_58_2_64 = chef_simon_wire_waypoint
  wp_60_0_65 = chef_simon_wire_waypoint
  wp_61_1_66 = chef_simon_wire_waypoint
  wp_62_2_67 = chef_simon_wire_waypoint
  wp_64_0_68 = chef_simon_wire_waypoint
  wp_65_1_69 = chef_simon_wire_waypoint
  wp_66_2_70 = chef_simon_wire_waypoint
  wp_68_0_71 = chef_simon_wire_waypoint
  wp_69_1_72 = chef_simon_wire_waypoint
  wp_70_2_73 = chef_simon_wire_waypoint
  wp_72_0_74 = chef_simon_wire_waypoint
  wp_74_0_75 = chef_simon_wire_waypoint
  wp_76_0_76 = chef_simon_wire_waypoint
  wp_77_1_77 = chef_simon_wire_waypoint
  wp_78_2_78 = chef_simon_wire_waypoint
  wp_80_0_79 = chef_simon_wire_waypoint
  wp_81_1_80 = chef_simon_wire_waypoint
  wp_82_2_81 = chef_simon_wire_waypoint
  R3_1k_gate = 1k Ω Resistor [Resistance=1k package=THT]
  R3_10k_gate_pulldown = 10k Ω Resistor [Resistance=10k package=THT]
  Q3_IRFB11N50APBF = Basic FET N-Channel [package="TO220 [THT]"]
  BTN3_4-terminal_plug = Camdenboss CTB0158-4 [part_number=CTB0158-4 package=THT]
  Ingredient_3_arcade_button_visual = Arcade Button (white)
  BTN3_local_GND_bus = chef_simon_local_ground_bus
  wp_84_0_91 = chef_simon_wire_waypoint
  wp_85_1_92 = chef_simon_wire_waypoint
  wp_86_2_93 = chef_simon_wire_waypoint
  wp_88_0_94 = chef_simon_wire_waypoint
  wp_89_1_95 = chef_simon_wire_waypoint
  wp_90_2_96 = chef_simon_wire_waypoint
  wp_92_0_97 = chef_simon_wire_waypoint
  wp_94_0_98 = chef_simon_wire_waypoint
  wp_96_0_99 = chef_simon_wire_waypoint
  wp_97_1_100 = chef_simon_wire_waypoint
  wp_98_2_101 = chef_simon_wire_waypoint
  wp_100_0_102 = chef_simon_wire_waypoint
  wp_101_1_103 = chef_simon_wire_waypoint
  wp_102_2_104 = chef_simon_wire_waypoint
  wp_104_0_105 = chef_simon_wire_waypoint
  wp_105_1_106 = chef_simon_wire_waypoint
  wp_106_2_107 = chef_simon_wire_waypoint
  wp_108_0_108 = chef_simon_wire_waypoint
  wp_109_1_109 = chef_simon_wire_waypoint
  wp_110_2_110 = chef_simon_wire_waypoint
  wp_112_0_111 = chef_simon_wire_waypoint
  wp_114_0_112 = chef_simon_wire_waypoint
  wp_116_0_113 = chef_simon_wire_waypoint
  wp_117_1_114 = chef_simon_wire_waypoint
  wp_118_2_115 = chef_simon_wire_waypoint
  wp_120_0_116 = chef_simon_wire_waypoint
  wp_121_1_117 = chef_simon_wire_waypoint
  wp_122_2_118 = chef_simon_wire_waypoint
  R4_1k_gate = 1k Ω Resistor [Resistance=1k package=THT]
  R4_10k_gate_pulldown = 10k Ω Resistor [Resistance=10k package=THT]
  Q4_IRFB11N50APBF = Basic FET N-Channel [package="TO220 [THT]"]
  BTN4_4-terminal_plug = Camdenboss CTB0158-4 [part_number=CTB0158-4 package=THT]
  Ingredient_4_arcade_button_visual = Arcade Button (yellow)
  BTN4_local_GND_bus = chef_simon_local_ground_bus
  wp_124_0_128 = chef_simon_wire_waypoint
  wp_125_1_129 = chef_simon_wire_waypoint
  wp_126_2_130 = chef_simon_wire_waypoint
  wp_128_0_131 = chef_simon_wire_waypoint
  wp_129_1_132 = chef_simon_wire_waypoint
  wp_130_2_133 = chef_simon_wire_waypoint
  wp_132_0_134 = chef_simon_wire_waypoint
  wp_134_0_135 = chef_simon_wire_waypoint
  wp_136_0_136 = chef_simon_wire_waypoint
  wp_137_1_137 = chef_simon_wire_waypoint
  wp_138_2_138 = chef_simon_wire_waypoint
  wp_140_0_139 = chef_simon_wire_waypoint
  wp_141_1_140 = chef_simon_wire_waypoint
  wp_142_2_141 = chef_simon_wire_waypoint
  wp_144_0_142 = chef_simon_wire_waypoint
  wp_145_1_143 = chef_simon_wire_waypoint
  wp_146_2_144 = chef_simon_wire_waypoint
  wp_148_0_145 = chef_simon_wire_waypoint
  wp_149_1_146 = chef_simon_wire_waypoint
  wp_150_2_147 = chef_simon_wire_waypoint
  wp_152_0_148 = chef_simon_wire_waypoint
  wp_154_0_149 = chef_simon_wire_waypoint
  wp_156_0_150 = chef_simon_wire_waypoint
  wp_157_1_151 = chef_simon_wire_waypoint
  wp_158_2_152 = chef_simon_wire_waypoint
  wp_160_0_153 = chef_simon_wire_waypoint
  wp_161_1_154 = chef_simon_wire_waypoint
  wp_162_2_155 = chef_simon_wire_waypoint
  R5_1k_gate = 1k Ω Resistor [Resistance=1k package=THT]
  R5_10k_gate_pulldown = 10k Ω Resistor [Resistance=10k package=THT]
  Q5_IRFB11N50APBF = Basic FET N-Channel [package="TO220 [THT]"]
  BTN5_4-terminal_plug = Camdenboss CTB0158-4 [part_number=CTB0158-4 package=THT]
  Ingredient_5_arcade_button_visual = Arcade Button (blue)
  BTN5_local_GND_bus = chef_simon_local_ground_bus
  wp_164_0_165 = chef_simon_wire_waypoint
  wp_165_1_166 = chef_simon_wire_waypoint
  wp_166_2_167 = chef_simon_wire_waypoint
  wp_168_0_168 = chef_simon_wire_waypoint
  wp_169_1_169 = chef_simon_wire_waypoint
  wp_170_2_170 = chef_simon_wire_waypoint
  wp_172_0_171 = chef_simon_wire_waypoint
  wp_174_0_172 = chef_simon_wire_waypoint
  wp_176_0_173 = chef_simon_wire_waypoint
  wp_177_1_174 = chef_simon_wire_waypoint
  wp_178_2_175 = chef_simon_wire_waypoint
  wp_180_0_176 = chef_simon_wire_waypoint
  wp_181_1_177 = chef_simon_wire_waypoint
  wp_182_2_178 = chef_simon_wire_waypoint
  wp_184_0_179 = chef_simon_wire_waypoint
  wp_185_1_180 = chef_simon_wire_waypoint
  wp_186_2_181 = chef_simon_wire_waypoint
  wp_188_0_182 = chef_simon_wire_waypoint
  wp_189_1_183 = chef_simon_wire_waypoint
  wp_190_2_184 = chef_simon_wire_waypoint
  wp_192_0_185 = chef_simon_wire_waypoint
  wp_194_0_186 = chef_simon_wire_waypoint
  wp_196_0_187 = chef_simon_wire_waypoint
  wp_197_1_188 = chef_simon_wire_waypoint
  wp_198_2_189 = chef_simon_wire_waypoint
  wp_200_0_190 = chef_simon_wire_waypoint
  wp_201_1_191 = chef_simon_wire_waypoint
  wp_202_2_192 = chef_simon_wire_waypoint

nets:
  N1: DOIT_ESP32_DevKit_V1.connector1, Common_GND_rail.tap0, wp_0_0_5.pin, wp_1_1_6.pin, wp_2_2_7.pin
  N2: DOIT_ESP32_DevKit_V1.connector5, BTN1_4-terminal_plug.pin3, Ingredient_1_arcade_button_visual.no_name_yet#1, wp_16_0_25.pin, wp_17_1_26.pin, wp_18_2_27.pin, wp_36_0_39.pin, wp_37_1_40.pin, wp_38_2_41.pin
  N3: DOIT_ESP32_DevKit_V1.connector6, BTN2_4-terminal_plug.pin3, Ingredient_2_arcade_button_visual.connector1, wp_56_0_62.pin, wp_57_1_63.pin, wp_58_2_64.pin, wp_76_0_76.pin, wp_77_1_77.pin, wp_78_2_78.pin
  N4: DOIT_ESP32_DevKit_V1.connector8, BTN3_4-terminal_plug.pin3, Ingredient_3_arcade_button_visual.no_name_yet#1, wp_96_0_99.pin, wp_97_1_100.pin, wp_98_2_101.pin, wp_116_0_113.pin, wp_117_1_114.pin, wp_118_2_115.pin
  N5: DOIT_ESP32_DevKit_V1.connector9, BTN4_4-terminal_plug.pin3, Ingredient_4_arcade_button_visual.no_name_yet#1, wp_136_0_136.pin, wp_137_1_137.pin, wp_138_2_138.pin, wp_156_0_150.pin, wp_157_1_151.pin, wp_158_2_152.pin
  N6: DOIT_ESP32_DevKit_V1.connector10, R1_1k_gate.Pin_0, wp_20_0_28.pin, wp_21_1_29.pin, wp_22_2_30.pin
  N7: DOIT_ESP32_DevKit_V1.connector13, R2_1k_gate.Pin_0, wp_60_0_65.pin, wp_61_1_66.pin, wp_62_2_67.pin
  N8: DOIT_ESP32_DevKit_V1.connector14, R3_1k_gate.Pin_0, wp_100_0_102.pin, wp_101_1_103.pin, wp_102_2_104.pin
  N9: DOIT_ESP32_DevKit_V1.connector22, R4_1k_gate.Pin_0, wp_140_0_139.pin, wp_141_1_140.pin, wp_142_2_141.pin
  N10: DOIT_ESP32_DevKit_V1.connector23, BTN5_4-terminal_plug.pin3, Ingredient_5_arcade_button_visual.no_name_yet#1, wp_176_0_173.pin, wp_177_1_174.pin, wp_178_2_175.pin, wp_196_0_187.pin, wp_197_1_188.pin, wp_198_2_189.pin
  N11: DOIT_ESP32_DevKit_V1.connector24, R5_1k_gate.Pin_0, wp_180_0_176.pin, wp_181_1_177.pin, wp_182_2_178.pin
  N12: +12V_LED_rail.tap1, BTN1_4-terminal_plug.pin1, wp_4_0_17.pin, wp_5_1_18.pin, wp_6_2_19.pin
  N13: +12V_LED_rail.tap2, BTN2_4-terminal_plug.pin1, wp_44_0_54.pin, wp_45_1_55.pin, wp_46_2_56.pin
  N14: +12V_LED_rail.tap3, BTN3_4-terminal_plug.pin1, wp_84_0_91.pin, wp_85_1_92.pin, wp_86_2_93.pin
  N15: +12V_LED_rail.tap4, BTN4_4-terminal_plug.pin1, wp_124_0_128.pin, wp_125_1_129.pin, wp_126_2_130.pin
  N16: +12V_LED_rail.tap5, BTN5_4-terminal_plug.pin1, wp_164_0_165.pin, wp_165_1_166.pin, wp_166_2_167.pin
  N17: Common_GND_rail.tap16, BTN1_local_GND_bus.tap5, wp_34_0_38.pin
  N18: Common_GND_rail.tap17, BTN2_local_GND_bus.tap5, wp_74_0_75.pin
  N19: Common_GND_rail.tap18, BTN3_local_GND_bus.tap5, wp_114_0_112.pin
  N20: Common_GND_rail.tap19, BTN4_local_GND_bus.tap5, wp_154_0_149.pin
  N21: Common_GND_rail.tap20, BTN5_local_GND_bus.tap5, wp_194_0_186.pin
  N22: R1_1k_gate.Pin_1, R1_10k_gate_pulldown.Pin_0, Q1_IRFB11N50APBF.gate, wp_24_0_31.pin, wp_25_1_32.pin, wp_26_2_33.pin, wp_28_0_34.pin, wp_29_1_35.pin, wp_30_2_36.pin
  N23: R1_10k_gate_pulldown.Pin_1, BTN1_local_GND_bus.tap0, wp_32_0_37.pin
  N24: Q1_IRFB11N50APBF.drain, BTN1_4-terminal_plug.pin2, wp_8_0_20.pin, wp_9_1_21.pin, wp_10_2_22.pin
  N25: Q1_IRFB11N50APBF.source, BTN1_local_GND_bus.tap1, wp_12_0_23.pin
  N26: BTN1_4-terminal_plug.pin4, Ingredient_1_arcade_button_visual.no_name_yet#2, BTN1_local_GND_bus.tap4, wp_14_0_24.pin, wp_40_0_42.pin, wp_41_1_43.pin, wp_42_2_44.pin
  N27: R2_1k_gate.Pin_1, R2_10k_gate_pulldown.Pin_0, Q2_IRFB11N50APBF.gate, wp_64_0_68.pin, wp_65_1_69.pin, wp_66_2_70.pin, wp_68_0_71.pin, wp_69_1_72.pin, wp_70_2_73.pin
  N28: R2_10k_gate_pulldown.Pin_1, BTN2_local_GND_bus.tap0, wp_72_0_74.pin
  N29: Q2_IRFB11N50APBF.drain, BTN2_4-terminal_plug.pin2, wp_48_0_57.pin, wp_49_1_58.pin, wp_50_2_59.pin
  N30: Q2_IRFB11N50APBF.source, BTN2_local_GND_bus.tap1, wp_52_0_60.pin
  N31: BTN2_4-terminal_plug.pin4, Ingredient_2_arcade_button_visual.connector2, BTN2_local_GND_bus.tap4, wp_54_0_61.pin, wp_80_0_79.pin, wp_81_1_80.pin, wp_82_2_81.pin
  N32: R3_1k_gate.Pin_1, R3_10k_gate_pulldown.Pin_0, Q3_IRFB11N50APBF.gate, wp_104_0_105.pin, wp_105_1_106.pin, wp_106_2_107.pin, wp_108_0_108.pin, wp_109_1_109.pin, wp_110_2_110.pin
  N33: R3_10k_gate_pulldown.Pin_1, BTN3_local_GND_bus.tap0, wp_112_0_111.pin
  N34: Q3_IRFB11N50APBF.drain, BTN3_4-terminal_plug.pin2, wp_88_0_94.pin, wp_89_1_95.pin, wp_90_2_96.pin
  N35: Q3_IRFB11N50APBF.source, BTN3_local_GND_bus.tap1, wp_92_0_97.pin
  N36: BTN3_4-terminal_plug.pin4, Ingredient_3_arcade_button_visual.no_name_yet#2, BTN3_local_GND_bus.tap4, wp_94_0_98.pin, wp_120_0_116.pin, wp_121_1_117.pin, wp_122_2_118.pin
  N37: R4_1k_gate.Pin_1, R4_10k_gate_pulldown.Pin_0, Q4_IRFB11N50APBF.gate, wp_144_0_142.pin, wp_145_1_143.pin, wp_146_2_144.pin, wp_148_0_145.pin, wp_149_1_146.pin, wp_150_2_147.pin
  N38: R4_10k_gate_pulldown.Pin_1, BTN4_local_GND_bus.tap0, wp_152_0_148.pin
  N39: Q4_IRFB11N50APBF.drain, BTN4_4-terminal_plug.pin2, wp_128_0_131.pin, wp_129_1_132.pin, wp_130_2_133.pin
  N40: Q4_IRFB11N50APBF.source, BTN4_local_GND_bus.tap1, wp_132_0_134.pin
  N41: BTN4_4-terminal_plug.pin4, Ingredient_4_arcade_button_visual.no_name_yet#2, BTN4_local_GND_bus.tap4, wp_134_0_135.pin, wp_160_0_153.pin, wp_161_1_154.pin, wp_162_2_155.pin
  N42: R5_1k_gate.Pin_1, R5_10k_gate_pulldown.Pin_0, Q5_IRFB11N50APBF.gate, wp_184_0_179.pin, wp_185_1_180.pin, wp_186_2_181.pin, wp_188_0_182.pin, wp_189_1_183.pin, wp_190_2_184.pin
  N43: R5_10k_gate_pulldown.Pin_1, BTN5_local_GND_bus.tap0, wp_192_0_185.pin
  N44: Q5_IRFB11N50APBF.drain, BTN5_4-terminal_plug.pin2, wp_168_0_168.pin, wp_169_1_169.pin, wp_170_2_170.pin
  N45: Q5_IRFB11N50APBF.source, BTN5_local_GND_bus.tap1, wp_172_0_171.pin
  N46: BTN5_4-terminal_plug.pin4, Ingredient_5_arcade_button_visual.no_name_yet#2, BTN5_local_GND_bus.tap4, wp_174_0_172.pin, wp_200_0_190.pin, wp_201_1_191.pin, wp_202_2_192.pin
