# Fritzing sketch chef_station_simon_library_art_editable (saved by Fritzing 1.0.7)

parts:
  DOIT_ESP32_DevKit_V1 = esp32_p30_w11 [part_number=ESP32S-PIN30]
  +12V_LED_rail = chef_simon_vplus_12v_rail
  Common_GND_rail = chef_simon_common_ground_rail
  R1_100_ohm_gate = Resistor [Resistance=100 tolerance=±5% power=0.25W resistance=220 package=THT]
  R1_10k_gate_pulldown = Resistor [Resistance=10k tolerance=±5% power=0.25W resistance=220 package=THT]
  Q1_IRFB11N50APBF = Basic FET N-Channel [package="TO220 [THT]"]
  BTN1_4-terminal_plug = Camdenboss CTB0158-4 [part_number=CTB0158-4 package=THT]
  Ingredient_1_arcade_button_visual = Arcade Button (red)
  R2_100_ohm_gate = Resistor [Resistance=100 tolerance=±5% power=0.25W resistance=220 package=THT]
  R2_10k_gate_pulldown = Resistor [Resistance=10k tolerance=±5% power=0.25W resistance=220 package=THT]
  Q2_IRFB11N50APBF = Basic FET N-Channel [package="TO220 [THT]"]
  BTN2_4-terminal_plug = Camdenboss CTB0158-4 [part_number=CTB0158-4 package=THT]
  Ingredient_2_arcade_button_visual = chef_simon_library_derived_green_arcade_button
  R3_100_ohm_gate = Resistor [Resistance=100 tolerance=±5% power=0.25W resistance=220 package=THT]
  R3_10k_gate_pulldown = Resistor [Resistance=10k tolerance=±5% power=0.25W resistance=220 package=THT]
  Q3_IRFB11N50APBF = Basic FET N-Channel [package="TO220 [THT]"]
  BTN3_4-terminal_plug = Camdenboss CTB0158-4 [part_number=CTB0158-4 package=THT]
  Ingredient_3_arcade_button_visual = Arcade Button (white)
  R4_100_ohm_gate = Resistor [Resistance=100 tolerance=±5% power=0.25W resistance=220 package=THT]
  R4_10k_gate_pulldown = Resistor [Resistance=10k tolerance=±5% power=0.25W resistance=220 package=THT]
  Q4_IRFB11N50APBF = Basic FET N-Channel [package="TO220 [THT]"]
  BTN4_4-terminal_plug = Camdenboss CTB0158-4 [part_number=CTB0158-4 package=THT]
  Ingredient_4_arcade_button_visual = Arcade Button (yellow)
  R5_100_ohm_gate = Resistor [Resistance=100 tolerance=±5% power=0.25W resistance=220 package=THT]
  R5_10k_gate_pulldown = Resistor [Resistance=10k tolerance=±5% power=0.25W resistance=220 package=THT]
  Q5_IRFB11N50APBF = Basic FET N-Channel [package="TO220 [THT]"]
  BTN5_4-terminal_plug = Camdenboss CTB0158-4 [part_number=CTB0158-4 package=THT]
  Ingredient_5_arcade_button_visual = Arcade Button (blue)

nets:
  N1: DOIT_ESP32_DevKit_V1.connector5, BTN1_4-terminal_plug.pin3, Ingredient_1_arcade_button_visual.no_name_yet#1
  N2: DOIT_ESP32_DevKit_V1.connector6, BTN2_4-terminal_plug.pin3, Ingredient_2_arcade_button_visual.connector1
  N3: DOIT_ESP32_DevKit_V1.connector8, BTN3_4-terminal_plug.pin3, Ingredient_3_arcade_button_visual.no_name_yet#1
  N4: DOIT_ESP32_DevKit_V1.connector9, BTN4_4-terminal_plug.pin3, Ingredient_4_arcade_button_visual.no_name_yet#1
  N5: DOIT_ESP32_DevKit_V1.connector10, R1_100_ohm_gate.Pin_0
  N6: DOIT_ESP32_DevKit_V1.connector13, R2_100_ohm_gate.Pin_0
  N7: DOIT_ESP32_DevKit_V1.connector14, R3_100_ohm_gate.Pin_0
  N8: DOIT_ESP32_DevKit_V1.connector22, R4_100_ohm_gate.Pin_0
  N9: DOIT_ESP32_DevKit_V1.connector23, BTN5_4-terminal_plug.pin3, Ingredient_5_arcade_button_visual.no_name_yet#1
  N10: DOIT_ESP32_DevKit_V1.connector24, R5_100_ohm_gate.Pin_0
  N11: +12V_LED_rail.tap1, BTN1_4-terminal_plug.pin1
  N12: +12V_LED_rail.tap2, BTN2_4-terminal_plug.pin1
  N13: +12V_LED_rail.tap3, BTN3_4-terminal_plug.pin1
  N14: +12V_LED_rail.tap4, BTN4_4-terminal_plug.pin1
  N15: +12V_LED_rail.tap5, BTN5_4-terminal_plug.pin1
  N16: Common_GND_rail.tap2, Q1_IRFB11N50APBF.source
  N17: Common_GND_rail.tap3, R1_10k_gate_pulldown.Pin_1, Q2_IRFB11N50APBF.source
  N18: Common_GND_rail.tap4, R2_10k_gate_pulldown.Pin_1, Q3_IRFB11N50APBF.source
  N19: Common_GND_rail.tap5, R3_10k_gate_pulldown.Pin_1, Q4_IRFB11N50APBF.source
  N20: Common_GND_rail.tap6, R4_10k_gate_pulldown.Pin_1, Q5_IRFB11N50APBF.source
  N21: Common_GND_rail.tap7, BTN1_4-terminal_plug.pin4, Ingredient_1_arcade_button_visual.no_name_yet#2, R5_10k_gate_pulldown.Pin_1
  N22: Common_GND_rail.tap8, BTN2_4-terminal_plug.pin4, Ingredient_2_arcade_button_visual.connector2
  N23: Common_GND_rail.tap9, BTN3_4-terminal_plug.pin4, Ingredient_3_arcade_button_visual.no_name_yet#2
  N24: Common_GND_rail.tap10, BTN4_4-terminal_plug.pin4, Ingredient_4_arcade_button_visual.no_name_yet#2
  N25: Common_GND_rail.tap11, BTN5_4-terminal_plug.pin4, Ingredient_5_arcade_button_visual.no_name_yet#2
  N26: R1_100_ohm_gate.Pin_1, R1_10k_gate_pulldown.Pin_0, Q1_IRFB11N50APBF.gate
  N27: Q1_IRFB11N50APBF.drain, BTN1_4-terminal_plug.pin2
  N28: R2_100_ohm_gate.Pin_1, R2_10k_gate_pulldown.Pin_0, Q2_IRFB11N50APBF.gate
  N29: Q2_IRFB11N50APBF.drain, BTN2_4-terminal_plug.pin2
  N30: R3_100_ohm_gate.Pin_1, R3_10k_gate_pulldown.Pin_0, Q3_IRFB11N50APBF.gate
  N31: Q3_IRFB11N50APBF.drain, BTN3_4-terminal_plug.pin2
  N32: R4_100_ohm_gate.Pin_1, R4_10k_gate_pulldown.Pin_0, Q4_IRFB11N50APBF.gate
  N33: Q4_IRFB11N50APBF.drain, BTN4_4-terminal_plug.pin2
  N34: R5_100_ohm_gate.Pin_1, R5_10k_gate_pulldown.Pin_0, Q5_IRFB11N50APBF.gate
  N35: Q5_IRFB11N50APBF.drain, BTN5_4-terminal_plug.pin2
