# Fritzing sketch chef_station_simon_library_art_resistor_values_editable (saved by Fritzing 1.0.3)

parts:
  DOIT_ESP32_DevKit_V1 = DOIT Esp32 DevKit v1 (30 pins long, 11 pins width)
  +12V_LED_rail = +12V lamp rail
  Common_GND_rail = Common ground rail
  Notes = Notes  # not connected
  ESP32_GPIOs = ESP32 GPIOs  # not connected
  R1_1k_gate = 1k Ω Resistor [Resistance=1k package=THT]
  R1_10k_gate_pulldown = 10k Ω Resistor [Resistance=10k package=THT]
  Q1_IRFB11N50APBF = Basic FET N-Channel [package="TO220 [THT]"]
  BTN1_4-terminal_plug = Camdenboss CTB0158-4 [package=THT]
  Ingredient_1_arcade_button_visual = Arcade Button (red)
  BTN1_plug_order = BTN1 plug order  # not connected
  BTN1_resistors = BTN1 resistors  # not connected
  Q1_G_/_D_/_S = Q1 G / D / S  # not connected
  R2_1k_gate = 1k Ω Resistor [Resistance=1k package=THT]
  R2_10k_gate_pulldown = 10k Ω Resistor [Resistance=10k package=THT]
  Q2_IRFB11N50APBF = Basic FET N-Channel [package="TO220 [THT]"]
  BTN2_4-terminal_plug = Camdenboss CTB0158-4 [package=THT]
  Ingredient_2_arcade_button_visual = Arcade Button (green, library-art derived)
  BTN2_plug_order = BTN2 plug order  # not connected
  BTN2_resistors = BTN2 resistors  # not connected
  Q2_G_/_D_/_S = Q2 G / D / S  # not connected
  R3_1k_gate = 1k Ω Resistor [Resistance=1k package=THT]
  R3_10k_gate_pulldown = 10k Ω Resistor [Resistance=10k package=THT]
  Q3_IRFB11N50APBF = Basic FET N-Channel [package="TO220 [THT]"]
  BTN3_4-terminal_plug = Camdenboss CTB0158-4 [package=THT]
  Ingredient_3_arcade_button_visual = Arcade Button (white)
  BTN3_plug_order = BTN3 plug order  # not connected
  BTN3_resistors = BTN3 resistors  # not connected
  Q3_G_/_D_/_S = Q3 G / D / S  # not connected
  R4_1k_gate = 1k Ω Resistor [Resistance=1k package=THT]
  R4_10k_gate_pulldown = 10k Ω Resistor [Resistance=10k package=THT]
  Q4_IRFB11N50APBF = Basic FET N-Channel [package="TO220 [THT]"]
  BTN4_4-terminal_plug = Camdenboss CTB0158-4 [package=THT]
  Ingredient_4_arcade_button_visual = Arcade Button (yellow)
  BTN4_plug_order = BTN4 plug order  # not connected
  BTN4_resistors = BTN4 resistors  # not connected
  Q4_G_/_D_/_S = Q4 G / D / S  # not connected
  R5_1k_gate = 1k Ω Resistor [Resistance=1k package=THT]
  R5_10k_gate_pulldown = 10k Ω Resistor [Resistance=10k package=THT]
  Q5_IRFB11N50APBF = Basic FET N-Channel [package="TO220 [THT]"]
  BTN5_4-terminal_plug = Camdenboss CTB0158-4 [package=THT]
  Ingredient_5_arcade_button_visual = Arcade Button (blue)
  BTN5_plug_order = BTN5 plug order  # not connected
  BTN5_resistors = BTN5 resistors  # not connected
  Q5_G_/_D_/_S = Q5 G / D / S  # not connected

nets:
  N1: DOIT_ESP32_DevKit_V1.RX2, BTN1_4-terminal_plug.pin3, Ingredient_1_arcade_button_visual.no_name_yet#1
  N2: DOIT_ESP32_DevKit_V1.TX2, BTN2_4-terminal_plug.pin3, Ingredient_2_arcade_button_visual.no_name_yet#1
  N3: DOIT_ESP32_DevKit_V1.D18, BTN3_4-terminal_plug.pin3, Ingredient_3_arcade_button_visual.no_name_yet#1
  N4: DOIT_ESP32_DevKit_V1.D19, BTN4_4-terminal_plug.pin3, Ingredient_4_arcade_button_visual.no_name_yet#1
  N5: DOIT_ESP32_DevKit_V1.D21, R1_1k_gate.Pin_0
  N6: DOIT_ESP32_DevKit_V1.D22, R2_1k_gate.Pin_0
  N7: DOIT_ESP32_DevKit_V1.D23, R3_1k_gate.Pin_0
  N8: DOIT_ESP32_DevKit_V1.D25, R4_1k_gate.Pin_0
  N9: DOIT_ESP32_DevKit_V1.D26, BTN5_4-terminal_plug.pin3, Ingredient_5_arcade_button_visual.no_name_yet#1
  N10: DOIT_ESP32_DevKit_V1.D27, R5_1k_gate.Pin_0
  N11: +12V_LED_rail.tap_1, +12V_LED_rail.tap_2, +12V_LED_rail.tap_3, +12V_LED_rail.tap_4, +12V_LED_rail.tap_5, BTN1_4-terminal_plug.pin1, BTN2_4-terminal_plug.pin1, BTN3_4-terminal_plug.pin1, BTN4_4-terminal_plug.pin1, BTN5_4-terminal_plug.pin1
  N12: Common_GND_rail.tap_2, Common_GND_rail.tap_3, Common_GND_rail.tap_4, Common_GND_rail.tap_5, Common_GND_rail.tap_6, Common_GND_rail.tap_7, Common_GND_rail.tap_8, Common_GND_rail.tap_9, Common_GND_rail.tap_10, Common_GND_rail.tap_11, R1_10k_gate_pulldown.Pin_1, Q1_IRFB11N50APBF.source, BTN1_4-terminal_plug.pin4, Ingredient_1_arcade_button_visual.no_name_yet#2, R2_10k_gate_pulldown.Pin_1, Q2_IRFB11N50APBF.source, BTN2_4-terminal_plug.pin4, Ingredient_2_arcade_button_visual.no_name_yet#2, R3_10k_gate_pulldown.Pin_1, Q3_IRFB11N50APBF.source, BTN3_4-terminal_plug.pin4, Ingredient_3_arcade_button_visual.no_name_yet#2, R4_10k_gate_pulldown.Pin_1, Q4_IRFB11N50APBF.source, BTN4_4-terminal_plug.pin4, Ingredient_4_arcade_button_visual.no_name_yet#2, R5_10k_gate_pulldown.Pin_1, Q5_IRFB11N50APBF.source, BTN5_4-terminal_plug.pin4, Ingredient_5_arcade_button_visual.no_name_yet#2
  N13: R1_1k_gate.Pin_1, R1_10k_gate_pulldown.Pin_0, Q1_IRFB11N50APBF.gate
  N14: Q1_IRFB11N50APBF.drain, BTN1_4-terminal_plug.pin2
  N15: R2_1k_gate.Pin_1, R2_10k_gate_pulldown.Pin_0, Q2_IRFB11N50APBF.gate
  N16: Q2_IRFB11N50APBF.drain, BTN2_4-terminal_plug.pin2
  N17: R3_1k_gate.Pin_1, R3_10k_gate_pulldown.Pin_0, Q3_IRFB11N50APBF.gate
  N18: Q3_IRFB11N50APBF.drain, BTN3_4-terminal_plug.pin2
  N19: R4_1k_gate.Pin_1, R4_10k_gate_pulldown.Pin_0, Q4_IRFB11N50APBF.gate
  N20: Q4_IRFB11N50APBF.drain, BTN4_4-terminal_plug.pin2
  N21: R5_1k_gate.Pin_1, R5_10k_gate_pulldown.Pin_0, Q5_IRFB11N50APBF.gate
  N22: Q5_IRFB11N50APBF.drain, BTN5_4-terminal_plug.pin2

custom parts:
  DOIT Esp32 DevKit v1 (30 pins long, 11 pins width): The DOIT Esp32 DevKit v1 is one of the development board created by DOIT to evaluate the ESP-WROOM-32 module. It is based on the ESP32 microcontroller that boasts Wifi, Bluetooth, Ethernet and Low Power support all in a single chip. (vanepp) made breadboard work, adjusted pin numbering and labels and reduced size of schematic and cleaned up pcb. This chip is 30pins long (2 x15) and 11 pins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
  Arcade Button (green, library-art derived): Adafruit Arcade Button (green, library-art derived)
