# Fritzing sketch chef_station_simon_4btn_audio_editable (saved by Fritzing 1.0.3)

parts:
  DOIT_ESP32_DevKit_V1 = DOIT Esp32 DevKit v1 (30 pins long, 11 pins width)
  +12V_LED_rail = +12V lamp rail
  +5V_PAM8403_rail = +5V amp rail
  Common_GND_rail = Common ground rail
  Notes = Notes  # not connected
  ESP32_GPIOs = ESP32 GPIOs  # not connected
  wp_0_0_6 = Wire waypoint
  wp_1_1_7 = Wire waypoint
  wp_2_2_8 = Wire waypoint
  R1_1k_gate = 1k Ω Resistor [Resistance=1k package=THT]
  R1_10k_gate_pulldown = 10k Ω Resistor [Resistance=10k package=THT]
  Q1_IRFB11N50APBF = Basic FET N-Channel [package="TO220 [THT]"]
  BTN1_4-terminal_plug = Camdenboss CTB0158-4 [package=THT]
  Ingredient_1_arcade_button_visual = Arcade Button (red)
  BTN1_local_GND_bus = Local GND bus
  BTN1_plug_order = BTN1 plug order  # not connected
  BTN1_resistors = BTN1 resistors  # not connected
  Q1_G_/_D_/_S = Q1 G / D / S  # not connected
  wp_4_0_18 = Wire waypoint
  wp_5_1_19 = Wire waypoint
  wp_6_2_20 = Wire waypoint
  wp_8_0_21 = Wire waypoint
  wp_9_1_22 = Wire waypoint
  wp_10_2_23 = Wire waypoint
  wp_12_0_24 = Wire waypoint
  wp_14_0_25 = Wire waypoint
  wp_16_0_26 = Wire waypoint
  wp_17_1_27 = Wire waypoint
  wp_18_2_28 = Wire waypoint
  wp_20_0_29 = Wire waypoint
  wp_21_1_30 = Wire waypoint
  wp_22_2_31 = Wire waypoint
  wp_24_0_32 = Wire waypoint
  wp_25_1_33 = Wire waypoint
  wp_26_2_34 = Wire waypoint
  wp_28_0_35 = Wire waypoint
  wp_29_1_36 = Wire waypoint
  wp_30_2_37 = Wire waypoint
  wp_32_0_38 = Wire waypoint
  wp_34_0_39 = Wire waypoint
  wp_36_0_40 = Wire waypoint
  wp_37_1_41 = Wire waypoint
  wp_38_2_42 = Wire waypoint
  wp_40_0_43 = Wire waypoint
  wp_41_1_44 = Wire waypoint
  wp_42_2_45 = Wire waypoint
  R2_1k_gate = 1k Ω Resistor [Resistance=1k package=THT]
  R2_10k_gate_pulldown = 10k Ω Resistor [Resistance=10k package=THT]
  Q2_IRFB11N50APBF = Basic FET N-Channel [package="TO220 [THT]"]
  BTN2_4-terminal_plug = Camdenboss CTB0158-4 [package=THT]
  Ingredient_2_arcade_button_visual = Arcade Button (green, library-art derived)
  BTN2_local_GND_bus = Local GND bus
  BTN2_plug_order = BTN2 plug order  # not connected
  BTN2_resistors = BTN2 resistors  # not connected
  Q2_G_/_D_/_S = Q2 G / D / S  # not connected
  wp_44_0_55 = Wire waypoint
  wp_45_1_56 = Wire waypoint
  wp_46_2_57 = Wire waypoint
  wp_48_0_58 = Wire waypoint
  wp_49_1_59 = Wire waypoint
  wp_50_2_60 = Wire waypoint
  wp_52_0_61 = Wire waypoint
  wp_54_0_62 = Wire waypoint
  wp_56_0_63 = Wire waypoint
  wp_57_1_64 = Wire waypoint
  wp_58_2_65 = Wire waypoint
  wp_60_0_66 = Wire waypoint
  wp_61_1_67 = Wire waypoint
  wp_62_2_68 = Wire waypoint
  wp_64_0_69 = Wire waypoint
  wp_65_1_70 = Wire waypoint
  wp_66_2_71 = Wire waypoint
  wp_68_0_72 = Wire waypoint
  wp_69_1_73 = Wire waypoint
  wp_70_2_74 = Wire waypoint
  wp_72_0_75 = Wire waypoint
  wp_74_0_76 = Wire waypoint
  wp_76_0_77 = Wire waypoint
  wp_77_1_78 = Wire waypoint
  wp_78_2_79 = Wire waypoint
  wp_80_0_80 = Wire waypoint
  wp_81_1_81 = Wire waypoint
  wp_82_2_82 = Wire waypoint
  R3_1k_gate = 1k Ω Resistor [Resistance=1k package=THT]
  R3_10k_gate_pulldown = 10k Ω Resistor [Resistance=10k package=THT]
  Q3_IRFB11N50APBF = Basic FET N-Channel [package="TO220 [THT]"]
  BTN3_4-terminal_plug = Camdenboss CTB0158-4 [package=THT]
  Ingredient_3_arcade_button_visual = Arcade Button (white)
  BTN3_local_GND_bus = Local GND bus
  BTN3_plug_order = BTN3 plug order  # not connected
  BTN3_resistors = BTN3 resistors  # not connected
  Q3_G_/_D_/_S = Q3 G / D / S  # not connected
  wp_84_0_92 = Wire waypoint
  wp_85_1_93 = Wire waypoint
  wp_86_2_94 = Wire waypoint
  wp_88_0_95 = Wire waypoint
  wp_89_1_96 = Wire waypoint
  wp_90_2_97 = Wire waypoint
  wp_92_0_98 = Wire waypoint
  wp_94_0_99 = Wire waypoint
  wp_96_0_100 = Wire waypoint
  wp_97_1_101 = Wire waypoint
  wp_98_2_102 = Wire waypoint
  wp_100_0_103 = Wire waypoint
  wp_101_1_104 = Wire waypoint
  wp_102_2_105 = Wire waypoint
  wp_104_0_106 = Wire waypoint
  wp_105_1_107 = Wire waypoint
  wp_106_2_108 = Wire waypoint
  wp_108_0_109 = Wire waypoint
  wp_109_1_110 = Wire waypoint
  wp_110_2_111 = Wire waypoint
  wp_112_0_112 = Wire waypoint
  wp_114_0_113 = Wire waypoint
  wp_116_0_114 = Wire waypoint
  wp_117_1_115 = Wire waypoint
  wp_118_2_116 = Wire waypoint
  wp_120_0_117 = Wire waypoint
  wp_121_1_118 = Wire waypoint
  wp_122_2_119 = Wire waypoint
  R4_1k_gate = 1k Ω Resistor [Resistance=1k package=THT]
  R4_10k_gate_pulldown = 10k Ω Resistor [Resistance=10k package=THT]
  Q4_IRFB11N50APBF = Basic FET N-Channel [package="TO220 [THT]"]
  BTN4_4-terminal_plug = Camdenboss CTB0158-4 [package=THT]
  Ingredient_4_arcade_button_visual = Arcade Button (yellow)
  BTN4_local_GND_bus = Local GND bus
  BTN4_plug_order = BTN4 plug order  # not connected
  BTN4_resistors = BTN4 resistors  # not connected
  Q4_G_/_D_/_S = Q4 G / D / S  # not connected
  wp_124_0_129 = Wire waypoint
  wp_125_1_130 = Wire waypoint
  wp_126_2_131 = Wire waypoint
  wp_128_0_132 = Wire waypoint
  wp_129_1_133 = Wire waypoint
  wp_130_2_134 = Wire waypoint
  wp_132_0_135 = Wire waypoint
  wp_134_0_136 = Wire waypoint
  wp_136_0_137 = Wire waypoint
  wp_137_1_138 = Wire waypoint
  wp_138_2_139 = Wire waypoint
  wp_140_0_140 = Wire waypoint
  wp_141_1_141 = Wire waypoint
  wp_142_2_142 = Wire waypoint
  wp_144_0_143 = Wire waypoint
  wp_145_1_144 = Wire waypoint
  wp_146_2_145 = Wire waypoint
  wp_148_0_146 = Wire waypoint
  wp_149_1_147 = Wire waypoint
  wp_150_2_148 = Wire waypoint
  wp_152_0_149 = Wire waypoint
  wp_154_0_150 = Wire waypoint
  wp_156_0_151 = Wire waypoint
  wp_157_1_152 = Wire waypoint
  wp_158_2_153 = Wire waypoint
  wp_160_0_154 = Wire waypoint
  wp_161_1_155 = Wire waypoint
  wp_162_2_156 = Wire waypoint
  Generic_PAM8403_5V_mini_amplifier = Generic PAM8403 5V mini amplifier
  SP1_4_ohm_/_3W_speaker = SPEAKER [Resistance="4 ohm" Power=3W package=pcb_mount_speaker]
  Audio_amp = Audio amp  # not connected
  wp_164_0_160 = Wire waypoint
  wp_165_1_161 = Wire waypoint
  wp_166_2_162 = Wire waypoint
  wp_168_0_163 = Wire waypoint
  wp_169_1_164 = Wire waypoint
  wp_170_2_165 = Wire waypoint
  wp_172_0_166 = Wire waypoint
  wp_173_1_167 = Wire waypoint
  wp_174_2_168 = Wire waypoint
  wp_176_0_169 = Wire waypoint
  wp_177_1_170 = Wire waypoint
  wp_178_2_171 = Wire waypoint
  wp_180_0_172 = Wire waypoint
  wp_181_1_173 = Wire waypoint
  wp_182_2_174 = Wire waypoint
  wp_184_0_175 = Wire waypoint
  wp_185_1_176 = Wire waypoint
  wp_186_2_177 = Wire waypoint

nets:
  N1: DOIT_ESP32_DevKit_V1.GND, Common_GND_rail.tap_0, Common_GND_rail.tap_12, Common_GND_rail.tap_13, Common_GND_rail.tap_16, Common_GND_rail.tap_17, Common_GND_rail.tap_18, Common_GND_rail.tap_19, wp_0_0_6.waypoint, wp_1_1_7.waypoint, wp_2_2_8.waypoint, R1_10k_gate_pulldown.Pin_1, Q1_IRFB11N50APBF.source, BTN1_4-terminal_plug.pin4, Ingredient_1_arcade_button_visual.no_name_yet#2, BTN1_local_GND_bus.ground_tap_0, BTN1_local_GND_bus.ground_tap_1, BTN1_local_GND_bus.ground_tap_4, BTN1_local_GND_bus.ground_tap_5, wp_12_0_24.waypoint, wp_14_0_25.waypoint, wp_32_0_38.waypoint, wp_34_0_39.waypoint, wp_40_0_43.waypoint, wp_41_1_44.waypoint, wp_42_2_45.waypoint, R2_10k_gate_pulldown.Pin_1, Q2_IRFB11N50APBF.source, BTN2_4-terminal_plug.pin4, Ingredient_2_arcade_button_visual.no_name_yet#2, BTN2_local_GND_bus.ground_tap_0, BTN2_local_GND_bus.ground_tap_1, BTN2_local_GND_bus.ground_tap_4, BTN2_local_GND_bus.ground_tap_5, wp_52_0_61.waypoint, wp_54_0_62.waypoint, wp_72_0_75.waypoint, wp_74_0_76.waypoint, wp_80_0_80.waypoint, wp_81_1_81.waypoint, wp_82_2_82.waypoint, R3_10k_gate_pulldown.Pin_1, Q3_IRFB11N50APBF.source, BTN3_4-terminal_plug.pin4, Ingredient_3_arcade_button_visual.no_name_yet#2, BTN3_local_GND_bus.ground_tap_0, BTN3_local_GND_bus.ground_tap_1, BTN3_local_GND_bus.ground_tap_4, BTN3_local_GND_bus.ground_tap_5, wp_92_0_98.waypoint, wp_94_0_99.waypoint, wp_112_0_112.waypoint, wp_114_0_113.waypoint, wp_120_0_117.waypoint, wp_121_1_118.waypoint, wp_122_2_119.waypoint, R4_10k_gate_pulldown.Pin_1, Q4_IRFB11N50APBF.source, BTN4_4-terminal_plug.pin4, Ingredient_4_arcade_button_visual.no_name_yet#2, BTN4_local_GND_bus.ground_tap_0, BTN4_local_GND_bus.ground_tap_1, BTN4_local_GND_bus.ground_tap_4, BTN4_local_GND_bus.ground_tap_5, wp_132_0_135.waypoint, wp_134_0_136.waypoint, wp_152_0_149.waypoint, wp_154_0_150.waypoint, wp_160_0_154.waypoint, wp_161_1_155.waypoint, wp_162_2_156.waypoint, Generic_PAM8403_5V_mini_amplifier.in_gnd, Generic_PAM8403_5V_mini_amplifier.pwr_gnd, wp_168_0_163.waypoint, wp_169_1_164.waypoint, wp_170_2_165.waypoint, wp_172_0_166.waypoint, wp_173_1_167.waypoint, wp_174_2_168.waypoint
  N2: DOIT_ESP32_DevKit_V1.RX2, BTN1_4-terminal_plug.pin3, Ingredient_1_arcade_button_visual.no_name_yet#1, wp_16_0_26.waypoint, wp_17_1_27.waypoint, wp_18_2_28.waypoint, wp_36_0_40.waypoint, wp_37_1_41.waypoint, wp_38_2_42.waypoint
  N3: DOIT_ESP32_DevKit_V1.TX2, BTN2_4-terminal_plug.pin3, Ingredient_2_arcade_button_visual.no_name_yet#1, wp_56_0_63.waypoint, wp_57_1_64.waypoint, wp_58_2_65.waypoint, wp_76_0_77.waypoint, wp_77_1_78.waypoint, wp_78_2_79.waypoint
  N4: DOIT_ESP32_DevKit_V1.D18, BTN3_4-terminal_plug.pin3, Ingredient_3_arcade_button_visual.no_name_yet#1, wp_96_0_100.waypoint, wp_97_1_101.waypoint, wp_98_2_102.waypoint, wp_116_0_114.waypoint, wp_117_1_115.waypoint, wp_118_2_116.waypoint
  N5: DOIT_ESP32_DevKit_V1.D19, BTN4_4-terminal_plug.pin3, Ingredient_4_arcade_button_visual.no_name_yet#1, wp_136_0_137.waypoint, wp_137_1_138.waypoint, wp_138_2_139.waypoint, wp_156_0_151.waypoint, wp_157_1_152.waypoint, wp_158_2_153.waypoint
  N6: DOIT_ESP32_DevKit_V1.D21, R1_1k_gate.Pin_0, wp_20_0_29.waypoint, wp_21_1_30.waypoint, wp_22_2_31.waypoint
  N7: DOIT_ESP32_DevKit_V1.D22, R2_1k_gate.Pin_0, wp_60_0_66.waypoint, wp_61_1_67.waypoint, wp_62_2_68.waypoint
  N8: DOIT_ESP32_DevKit_V1.D23, R3_1k_gate.Pin_0, wp_100_0_103.waypoint, wp_101_1_104.waypoint, wp_102_2_105.waypoint
  N9: DOIT_ESP32_DevKit_V1.D25, R4_1k_gate.Pin_0, wp_140_0_140.waypoint, wp_141_1_141.waypoint, wp_142_2_142.waypoint
  N10: DOIT_ESP32_DevKit_V1.D26, Generic_PAM8403_5V_mini_amplifier.lin, wp_176_0_169.waypoint, wp_177_1_170.waypoint, wp_178_2_171.waypoint
  N11: +12V_LED_rail.tap_1, +12V_LED_rail.tap_2, +12V_LED_rail.tap_3, +12V_LED_rail.tap_4, BTN1_4-terminal_plug.pin1, wp_4_0_18.waypoint, wp_5_1_19.waypoint, wp_6_2_20.waypoint, BTN2_4-terminal_plug.pin1, wp_44_0_55.waypoint, wp_45_1_56.waypoint, wp_46_2_57.waypoint, BTN3_4-terminal_plug.pin1, wp_84_0_92.waypoint, wp_85_1_93.waypoint, wp_86_2_94.waypoint, BTN4_4-terminal_plug.pin1, wp_124_0_129.waypoint, wp_125_1_130.waypoint, wp_126_2_131.waypoint
  N12: +5V_PAM8403_rail.tap_18, Generic_PAM8403_5V_mini_amplifier.vcc, wp_164_0_160.waypoint, wp_165_1_161.waypoint, wp_166_2_162.waypoint
  N13: R1_1k_gate.Pin_1, R1_10k_gate_pulldown.Pin_0, Q1_IRFB11N50APBF.gate, wp_24_0_32.waypoint, wp_25_1_33.waypoint, wp_26_2_34.waypoint, wp_28_0_35.waypoint, wp_29_1_36.waypoint, wp_30_2_37.waypoint
  N14: Q1_IRFB11N50APBF.drain, BTN1_4-terminal_plug.pin2, wp_8_0_21.waypoint, wp_9_1_22.waypoint, wp_10_2_23.waypoint
  N15: R2_1k_gate.Pin_1, R2_10k_gate_pulldown.Pin_0, Q2_IRFB11N50APBF.gate, wp_64_0_69.waypoint, wp_65_1_70.waypoint, wp_66_2_71.waypoint, wp_68_0_72.waypoint, wp_69_1_73.waypoint, wp_70_2_74.waypoint
  N16: Q2_IRFB11N50APBF.drain, BTN2_4-terminal_plug.pin2, wp_48_0_58.waypoint, wp_49_1_59.waypoint, wp_50_2_60.waypoint
  N17: R3_1k_gate.Pin_1, R3_10k_gate_pulldown.Pin_0, Q3_IRFB11N50APBF.gate, wp_104_0_106.waypoint, wp_105_1_107.waypoint, wp_106_2_108.waypoint, wp_108_0_109.waypoint, wp_109_1_110.waypoint, wp_110_2_111.waypoint
  N18: Q3_IRFB11N50APBF.drain, BTN3_4-terminal_plug.pin2, wp_88_0_95.waypoint, wp_89_1_96.waypoint, wp_90_2_97.waypoint
  N19: R4_1k_gate.Pin_1, R4_10k_gate_pulldown.Pin_0, Q4_IRFB11N50APBF.gate, wp_144_0_143.waypoint, wp_145_1_144.waypoint, wp_146_2_145.waypoint, wp_148_0_146.waypoint, wp_149_1_147.waypoint, wp_150_2_148.waypoint
  N20: Q4_IRFB11N50APBF.drain, BTN4_4-terminal_plug.pin2, wp_128_0_132.waypoint, wp_129_1_133.waypoint, wp_130_2_134.waypoint
  N21: Generic_PAM8403_5V_mini_amplifier.lminus, SP1_4_ohm_/_3W_speaker.+, wp_184_0_175.waypoint, wp_185_1_176.waypoint, wp_186_2_177.waypoint
  N22: Generic_PAM8403_5V_mini_amplifier.lplus, SP1_4_ohm_/_3W_speaker.-, wp_180_0_172.waypoint, wp_181_1_173.waypoint, wp_182_2_174.waypoint

custom parts:
  DOIT Esp32 DevKit v1 (30 pins long, 11 pins width): The DOIT Esp32 DevKit v1 is one of the development board created by DOIT to evaluate the ESP-WROOM-32 module. It is based on the ESP32 microcontroller that boasts Wifi, Bluetooth, Ethernet and Low Power support all in a single chip. (vanepp) made breadboard work, adjusted pin numbering and labels and reduced size of schematic and cleaned up pcb. This chip is 30pins long (2 x15) and 11 pins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
  Arcade Button (green, library-art derived): Adafruit Arcade Button (green, library-art derived)
