# Fritzing sketch chef_station_master_controller_score_print_editable (saved by Fritzing 1.0.3)

parts:
  Chef_Station_"Master_Controller_/_Score_+_Print_Layer" = Chef Station "Master Controller / Score + Print Layer"  # not connected
  Master_software_state_machine = Master software state machine  # not connected
  Raspberry_Pi_pin_summary = Raspberry Pi pin summary  # not connected
  FRONT_/_OPERATOR_CONTROL_EDGE = FRONT / OPERATOR CONTROL EDGE  # not connected
  Master_volume_is_a_software_control_signal = Master volume is a software control signal  # not connected
  LED_data_level_shifting = LED data level shifting  # not connected
  External_5V_LED_power = External 5V LED power  # not connected
  Common_ground = Common ground  # not connected
  Ethernet_module_communication = Ethernet module communication  # not connected
  No_hardware_sync_terminals = No hardware sync terminals  # not connected
  Epson_printer_connection = Epson printer connection  # not connected
  Local_controller_speaker = Local controller speaker  # not connected
  Score/status_messages_over_Ethernet_UDP_42100 = Score/status messages over Ethernet UDP 42100  # not connected
  Official_Raspberry_Pi_power_supply = Official Raspberry Pi power supply
  Raspberry_Pi_master_score/print_host = Raspberry Pi master score/print host
  USB_powered_local_controller_speaker = Local controller USB audio speaker
  +5V_LED_rail = +5V LED rail
  3_3V_logic_rail = 3.3V logic rail
  Common_logic_ground_rail = Common logic GND rail
  External_regulated_5V_LED_supply = External regulated 5V LED supply
  ADS1115_I2C_ADC_for_master_volume = ADS1115 I2C ADC for master volume
  Master_Volume_10k_linear_potentiometer = Master Volume 10k linear potentiometer
  Start_Game_momentary_pushbutton = Start Game momentary pushbutton
  Optional_C1_0_1uF_debounce_capacitor_across_Start_button = Optional 0.1uF hardware debounce capacitor [Capacitance=0.1uF]
  74AHCT125_LED_data_level_shifter = 74AHCT125 / 74HCT245 LED data level shifter
  R1_330-470_ohm_LED_data_resistor = 330-470 ohm LED data resistor [Resistance="330-470 ohm"]
  C2_1000uF_electrolytic_across_LED_strip_+5V/GND = 1000uF capacitor near LED strip [Capacitance=1000uF]
  Cooktop_overhead_WS2812B_/_NeoPixel_LED_strip = Cooktop overhead WS2812B / NeoPixel LED strip
  Module_Ethernet_/_UDP_network = MODULE ETHERNET / UDP NETWORK
  Simon_Module_Ethernet_connector = Simon Module bus connector
  Chopping_Module_Ethernet_connector = Chopping Module bus connector
  Pan_Motion_Module_Ethernet_connector = Pan Motion Module bus connector
  Pot_Temperature_Module_Ethernet_connector = Pot Temperature Module bus connector
  Garnish_Placement_Module_Ethernet_connector = Garnish Placement Module bus connector
  Epson_TM-T20IV_/_TM-T20V_receipt_printer = Epson TM-T20IV / TM-T20V-family receipt printer
  Epson_manufacturer_printer_power_supply = Epson manufacturer power supply
  R_+_B_Grill_score_receipt_preview = Receipt printout preview with R + B Grill logo placeholder  # not connected
  Breadboard_and_terminal_block_field = Breadboard / terminal block field  # not connected
  wp_0_0_39 = Wire waypoint
  wp_1_1_40 = Wire waypoint
  wp_3_0_41 = Wire waypoint
  wp_4_1_42 = Wire waypoint
  wp_6_0_43 = Wire waypoint
  wp_7_1_44 = Wire waypoint
  wp_9_0_45 = Wire waypoint
  wp_10_1_46 = Wire waypoint
  wp_12_0_47 = Wire waypoint
  wp_13_1_48 = Wire waypoint
  wp_15_0_49 = Wire waypoint
  wp_16_1_50 = Wire waypoint
  wp_18_1_51 = Wire waypoint
  wp_20_0_52 = Wire waypoint
  wp_21_1_53 = Wire waypoint
  wp_23_0_54 = Wire waypoint
  wp_24_1_55 = Wire waypoint
  wp_26_0_56 = Wire waypoint
  wp_27_1_57 = Wire waypoint
  wp_29_0_58 = Wire waypoint
  wp_30_1_59 = Wire waypoint
  wp_32_0_60 = Wire waypoint
  wp_33_1_61 = Wire waypoint
  wp_35_0_62 = Wire waypoint
  wp_36_1_63 = Wire waypoint
  wp_38_0_64 = Wire waypoint
  wp_39_1_65 = Wire waypoint
  wp_41_0_66 = Wire waypoint
  wp_42_1_67 = Wire waypoint
  wp_44_0_68 = Wire waypoint
  wp_45_1_69 = Wire waypoint
  wp_47_0_70 = Wire waypoint
  wp_48_1_71 = Wire waypoint
  wp_50_0_72 = Wire waypoint
  wp_51_1_73 = Wire waypoint
  wp_53_0_74 = Wire waypoint
  wp_54_1_75 = Wire waypoint
  wp_56_0_76 = Wire waypoint
  wp_57_1_77 = Wire waypoint
  wp_59_0_78 = Wire waypoint
  wp_60_1_79 = Wire waypoint
  wp_62_0_80 = Wire waypoint
  wp_63_1_81 = Wire waypoint
  wp_65_0_82 = Wire waypoint
  wp_66_1_83 = Wire waypoint
  wp_68_0_84 = Wire waypoint
  wp_69_1_85 = Wire waypoint
  wp_71_0_86 = Wire waypoint
  wp_72_1_87 = Wire waypoint
  wp_74_0_88 = Wire waypoint
  wp_75_1_89 = Wire waypoint
  wp_77_0_90 = Wire waypoint
  wp_78_1_91 = Wire waypoint
  wp_80_0_92 = Wire waypoint
  wp_81_1_93 = Wire waypoint
  wp_83_0_94 = Wire waypoint
  wp_84_1_95 = Wire waypoint
  wp_86_0_96 = Wire waypoint
  wp_87_1_97 = Wire waypoint
  wp_89_0_98 = Wire waypoint
  wp_90_1_99 = Wire waypoint
  wp_92_0_100 = Wire waypoint
  wp_93_1_101 = Wire waypoint
  wp_95_0_102 = Wire waypoint
  wp_96_1_103 = Wire waypoint
  wp_98_0_104 = Wire waypoint
  wp_99_1_105 = Wire waypoint
  wp_101_0_106 = Wire waypoint
  wp_102_1_107 = Wire waypoint
  wp_104_0_108 = Wire waypoint
  wp_105_1_109 = Wire waypoint

nets:
  N1: Official_Raspberry_Pi_power_supply.USB-C/micro-USB_output, Raspberry_Pi_master_score/print_host.Official_USB-C_power_in, wp_0_0_39.waypoint, wp_1_1_40.waypoint
  N2: Raspberry_Pi_master_score/print_host.Ethernet_to_module_network, Module_Ethernet_/_UDP_network.Chopping_Module_Ethernet/UDP_branch, Module_Ethernet_/_UDP_network.Ethernet_from_Pi/switch_module_network, Module_Ethernet_/_UDP_network.Garnish_Placement_Module_Ethernet/UDP_branch, Module_Ethernet_/_UDP_network.Pan_Motion_Module_Ethernet/UDP_branch, Module_Ethernet_/_UDP_network.Pot_Temperature_Module_Ethernet/UDP_branch, Module_Ethernet_/_UDP_network.Simon_Module_Ethernet/UDP_branch, Simon_Module_Ethernet_connector.Ethernet_/_UDP_module_command_link, Chopping_Module_Ethernet_connector.Ethernet_/_UDP_module_command_link, Pan_Motion_Module_Ethernet_connector.Ethernet_/_UDP_module_command_link, Pot_Temperature_Module_Ethernet_connector.Ethernet_/_UDP_module_command_link, Garnish_Placement_Module_Ethernet_connector.Ethernet_/_UDP_module_command_link, wp_12_0_47.waypoint, wp_13_1_48.waypoint, wp_92_0_100.waypoint, wp_93_1_101.waypoint, wp_95_0_102.waypoint, wp_96_1_103.waypoint, wp_98_0_104.waypoint, wp_99_1_105.waypoint, wp_101_0_106.waypoint, wp_102_1_107.waypoint, wp_104_0_108.waypoint, wp_105_1_109.waypoint
  GND: Raspberry_Pi_master_score/print_host.GND_to_common_logic_ground, Common_logic_ground_rail.Common_logic_GND_rail_tap_0, Common_logic_ground_rail.Common_logic_GND_rail_tap_2, Common_logic_ground_rail.Common_logic_GND_rail_tap_3, Common_logic_ground_rail.Common_logic_GND_rail_tap_4, Common_logic_ground_rail.Common_logic_GND_rail_tap_6, Common_logic_ground_rail.Common_logic_GND_rail_tap_7, Common_logic_ground_rail.Common_logic_GND_rail_tap_8, Common_logic_ground_rail.Common_logic_GND_rail_tap_12, Common_logic_ground_rail.Common_logic_GND_rail_tap_15, External_regulated_5V_LED_supply.GND, ADS1115_I2C_ADC_for_master_volume.ADDR_to_GND, ADS1115_I2C_ADC_for_master_volume.GND, Master_Volume_10k_linear_potentiometer.outer_lug_2_to_GND, Start_Game_momentary_pushbutton.button_GND, Optional_C1_0_1uF_debounce_capacitor_across_Start_button.button_GND_side, 74AHCT125_LED_data_level_shifter.GND, 74AHCT125_LED_data_level_shifter.OE_tied_to_GND, C2_1000uF_electrolytic_across_LED_strip_+5V/GND.negative, Cooktop_overhead_WS2812B_/_NeoPixel_LED_strip.GND_to_common_rail, wp_18_1_51.waypoint, wp_20_0_52.waypoint, wp_21_1_53.waypoint, wp_29_0_58.waypoint, wp_30_1_59.waypoint, wp_38_0_64.waypoint, wp_39_1_65.waypoint, wp_44_0_68.waypoint, wp_45_1_69.waypoint, wp_53_0_74.waypoint, wp_54_1_75.waypoint, wp_59_0_78.waypoint, wp_60_1_79.waypoint, wp_68_0_84.waypoint, wp_69_1_85.waypoint, wp_71_0_86.waypoint, wp_72_1_87.waypoint, wp_83_0_94.waypoint, wp_84_1_95.waypoint, wp_89_0_98.waypoint, wp_90_1_99.waypoint
  N3: Raspberry_Pi_master_score/print_host.GPIO2_/_SDA_to_ADS1115, ADS1115_I2C_ADC_for_master_volume.SDA_to_GPIO2, wp_32_0_60.waypoint, wp_33_1_61.waypoint
  N4: Raspberry_Pi_master_score/print_host.GPIO3_/_SCL_to_ADS1115, ADS1115_I2C_ADC_for_master_volume.SCL_to_GPIO3, wp_35_0_62.waypoint, wp_36_1_63.waypoint
  N5: Raspberry_Pi_master_score/print_host.GPIO5_Start_Game_input, Start_Game_momentary_pushbutton.GPIO5_button_input_active_LOW, Optional_C1_0_1uF_debounce_capacitor_across_Start_button.button_signal_side, wp_50_0_72.waypoint, wp_51_1_73.waypoint, wp_56_0_76.waypoint, wp_57_1_77.waypoint
  N6: Raspberry_Pi_master_score/print_host.GPIO18_LED_data, 74AHCT125_LED_data_level_shifter.A1_input_from_Raspberry_Pi_GPIO18, wp_62_0_80.waypoint, wp_63_1_81.waypoint
  N7: Raspberry_Pi_master_score/print_host.3.3V_logic_rail, 3_3V_logic_rail.3.3V_logic_rail_tap_0, 3_3V_logic_rail.3.3V_logic_rail_tap_2, 3_3V_logic_rail.3.3V_logic_rail_tap_3, ADS1115_I2C_ADC_for_master_volume.VDD_3.3V, Master_Volume_10k_linear_potentiometer.outer_lug_1_to_3.3V, wp_23_0_54.waypoint, wp_24_1_55.waypoint, wp_26_0_56.waypoint, wp_27_1_57.waypoint, wp_41_0_66.waypoint, wp_42_1_67.waypoint
  N8: Raspberry_Pi_master_score/print_host.USB_audio_dongle_/_powered_speaker, USB_powered_local_controller_speaker.USB_audio_from_Raspberry_Pi, wp_3_0_41.waypoint, wp_4_1_42.waypoint
  N9: Raspberry_Pi_master_score/print_host.USB_to_Epson_printer, Epson_TM-T20IV_/_TM-T20V_receipt_printer.USB_from_Raspberry_Pi, wp_6_0_43.waypoint, wp_7_1_44.waypoint
  N10: +5V_LED_rail.+5V_LED_rail_tap_7, +5V_LED_rail.+5V_LED_rail_tap_12, +5V_LED_rail.+5V_LED_rail_tap_15, External_regulated_5V_LED_supply.+5V, 74AHCT125_LED_data_level_shifter.VCC_5V, C2_1000uF_electrolytic_across_LED_strip_+5V/GND.positive, Cooktop_overhead_WS2812B_/_NeoPixel_LED_strip.+5V_from_external_LED_supply, wp_15_0_49.waypoint, wp_16_1_50.waypoint, wp_65_0_82.waypoint, wp_66_1_83.waypoint, wp_80_0_92.waypoint, wp_81_1_93.waypoint, wp_86_0_96.waypoint, wp_87_1_97.waypoint
  N11: ADS1115_I2C_ADC_for_master_volume.A0_volume_pot_wiper, Master_Volume_10k_linear_potentiometer.center_wiper_to_ADS1115_A0, wp_47_0_70.waypoint, wp_48_1_71.waypoint
  N12: 74AHCT125_LED_data_level_shifter.Y1_5V_data_output, R1_330-470_ohm_LED_data_resistor.lead_A, wp_74_0_88.waypoint, wp_75_1_89.waypoint
  N13: R1_330-470_ohm_LED_data_resistor.lead_B, Cooktop_overhead_WS2812B_/_NeoPixel_LED_strip.LED_DIN_from_level_shifter_through_resistor, wp_77_0_90.waypoint, wp_78_1_91.waypoint
  N14: Epson_TM-T20IV_/_TM-T20V_receipt_printer.Epson_power_input, Epson_manufacturer_printer_power_supply.printer_power_output, wp_9_0_45.waypoint, wp_10_1_46.waypoint
