# Fritzing sketch chef_station_master_power_network_editable (saved by Fritzing 1.0.3)

parts:
  Chef_Station_Master_Power_And_Network_Layout = Chef Station Master Power And Network Layout  # not connected
  Wire_color_legend = Wire color legend  # not connected
  AC_power_entry_/_power_strip = AC power entry / power strip
  LS108GP_manufacturer_power_adapter = LS108GP power adapter
  Epson_manufacturer_printer_PSU = Epson printer PSU
  Raspberry_Pi_official_PSU = Raspberry Pi official PSU
  Adjustable_12V_adapter_A = 12V Adapter A
  Adjustable_12V_adapter_D = 12V Adapter D
  Adjustable_12V_adapter_B = 12V Adapter B
  Adjustable_12V_adapter_C = 12V Adapter C
  TP-Link_LiteWave_LS108GP_8-port_PoE_switch = TP-Link LiteWave LS108GP PoE switch
  Optional_router_/_DHCP_source = Optional router / DHCP source
  Optional_Raspberry_Pi_master_controller_/_print_host = Optional Raspberry Pi master controller / print host
  Epson_receipt_printer = Epson TM-T20IV / TM-T20V-family receipt printer
  Buck_#1_optional_5V_AUX = Buck #1
  Buck_#2_5V_LED = Buck #2
  Buck_#3_5V_AUDIO_SERVO = Buck #3
  12V_SHOW_/_12V_ACTUAL_LOADS_terminal_block = 12V_SHOW / 12V ACTUAL LOADS
  5V_LED_terminal_block = 5V_LED
  5V_AUDIO_SERVO_terminal_block = 5V_AUDIO_SERVO
  5V_AUX_terminal_block = 5V_AUX
  COMMON_GND_distribution_terminal_block = COMMON_GND
  Simon_ESP32_PoE_board = Simon ESP32 PoE board
  Simon_local_accessory_terminal_block = Simon local accessory terminal block
  Chop_ESP32_PoE_board = Chopping ESP32 PoE board
  Chop_local_accessory_terminal_block = Chopping local accessory terminal block
  Pan_ESP32_PoE_board = Pan Motion ESP32 PoE board
  Pan_local_accessory_terminal_block = Pan Motion local accessory terminal block
  Pot_ESP32_PoE_board = Pot Temperature ESP32 PoE board
  Pot_local_accessory_terminal_block = Pot Temperature local accessory terminal block
  Garnish_ESP32_PoE_board = Garnish ESP32 PoE board
  Garnish_local_accessory_terminal_block = Garnish local accessory terminal block
  PoE_budget_table = PoE budget table  # not connected
  Power-source_table = Power-source table  # not connected
  Safety_and_separation_callouts = Safety and separation callouts  # not connected
  Grounding_rule = Grounding rule  # not connected
  Network_behavior = Network behavior  # not connected
  Setup_checklist_highlights = Setup checklist highlights  # not connected
  wp_0_0_38 = Wire waypoint
  wp_1_1_39 = Wire waypoint
  wp_3_0_40 = Wire waypoint
  wp_4_1_41 = Wire waypoint
  wp_6_0_42 = Wire waypoint
  wp_7_1_43 = Wire waypoint
  wp_9_0_44 = Wire waypoint
  wp_10_1_45 = Wire waypoint
  wp_12_0_46 = Wire waypoint
  wp_13_1_47 = Wire waypoint
  wp_15_0_48 = Wire waypoint
  wp_16_1_49 = Wire waypoint
  wp_18_0_50 = Wire waypoint
  wp_19_1_51 = Wire waypoint
  wp_21_0_52 = Wire waypoint
  wp_22_1_53 = Wire waypoint
  wp_24_0_54 = Wire waypoint
  wp_25_1_55 = Wire waypoint
  wp_27_0_56 = Wire waypoint
  wp_28_1_57 = Wire waypoint
  wp_30_0_58 = Wire waypoint
  wp_31_1_59 = Wire waypoint
  wp_33_0_60 = Wire waypoint
  wp_34_1_61 = Wire waypoint
  wp_36_0_62 = Wire waypoint
  wp_37_1_63 = Wire waypoint
  wp_39_0_64 = Wire waypoint
  wp_40_1_65 = Wire waypoint
  wp_42_0_66 = Wire waypoint
  wp_43_1_67 = Wire waypoint
  wp_45_0_68 = Wire waypoint
  wp_46_1_69 = Wire waypoint
  wp_47_2_70 = Wire waypoint
  wp_49_0_71 = Wire waypoint
  wp_50_1_72 = Wire waypoint
  wp_51_2_73 = Wire waypoint
  wp_53_0_74 = Wire waypoint
  wp_54_1_75 = Wire waypoint
  wp_56_0_76 = Wire waypoint
  wp_57_1_77 = Wire waypoint
  wp_58_2_78 = Wire waypoint
  wp_60_0_79 = Wire waypoint
  wp_61_1_80 = Wire waypoint
  wp_63_0_81 = Wire waypoint
  wp_64_1_82 = Wire waypoint
  wp_66_0_83 = Wire waypoint
  wp_67_1_84 = Wire waypoint
  wp_69_0_85 = Wire waypoint
  wp_70_1_86 = Wire waypoint
  wp_72_0_87 = Wire waypoint
  wp_73_1_88 = Wire waypoint
  wp_75_0_89 = Wire waypoint
  wp_76_1_90 = Wire waypoint
  wp_78_0_91 = Wire waypoint
  wp_79_1_92 = Wire waypoint
  wp_81_0_93 = Wire waypoint
  wp_82_1_94 = Wire waypoint
  wp_84_0_95 = Wire waypoint
  wp_85_1_96 = Wire waypoint
  wp_87_0_97 = Wire waypoint
  wp_88_1_98 = Wire waypoint
  wp_90_0_99 = Wire waypoint
  wp_91_1_100 = Wire waypoint
  wp_93_0_101 = Wire waypoint
  wp_94_1_102 = Wire waypoint
  wp_96_1_103 = Wire waypoint
  wp_98_0_104 = Wire waypoint
  wp_99_1_105 = Wire waypoint
  wp_101_0_106 = Wire waypoint
  wp_102_1_107 = Wire waypoint
  wp_104_0_108 = Wire waypoint
  wp_105_1_109 = Wire waypoint
  wp_107_0_110 = Wire waypoint
  wp_108_1_111 = Wire waypoint
  wp_110_0_112 = Wire waypoint
  wp_112_0_113 = Wire waypoint
  wp_114_0_114 = Wire waypoint
  wp_115_1_115 = Wire waypoint
  wp_117_0_116 = Wire waypoint
  wp_119_0_117 = Wire waypoint
  wp_121_0_118 = Wire waypoint
  wp_122_1_119 = Wire waypoint
  wp_124_0_120 = Wire waypoint
  wp_126_0_121 = Wire waypoint
  wp_128_0_122 = Wire waypoint
  wp_129_1_123 = Wire waypoint
  wp_131_0_124 = Wire waypoint
  wp_133_0_125 = Wire waypoint
  wp_135_0_126 = Wire waypoint
  wp_136_1_127 = Wire waypoint
  wp_138_0_128 = Wire waypoint
  wp_140_0_129 = Wire waypoint
  wp_142_0_130 = Wire waypoint
  wp_143_1_131 = Wire waypoint
  wp_145_0_132 = Wire waypoint
  wp_146_1_133 = Wire waypoint
  wp_148_0_134 = Wire waypoint
  wp_149_1_135 = Wire waypoint
  wp_151_0_136 = Wire waypoint
  wp_152_1_137 = Wire waypoint
  wp_154_0_138 = Wire waypoint
  wp_155_1_139 = Wire waypoint
  wp_157_0_140 = Wire waypoint
  wp_158_1_141 = Wire waypoint
  wp_160_0_142 = Wire waypoint
  wp_161_1_143 = Wire waypoint
  wp_163_0_144 = Wire waypoint
  wp_164_1_145 = Wire waypoint
  wp_166_0_146 = Wire waypoint
  wp_167_1_147 = Wire waypoint
  wp_169_0_148 = Wire waypoint
  wp_170_1_149 = Wire waypoint
  wp_172_0_150 = Wire waypoint
  wp_173_1_151 = Wire waypoint
  wp_175_0_152 = Wire waypoint
  wp_176_1_153 = Wire waypoint

nets:
  N1: AC_power_entry_/_power_strip.AC_to_12V_adapter_A, Adjustable_12V_adapter_A.AC_input, wp_9_0_44.waypoint, wp_10_1_45.waypoint
  N2: AC_power_entry_/_power_strip.AC_to_12V_adapter_B, Adjustable_12V_adapter_B.AC_input, wp_15_0_48.waypoint, wp_16_1_49.waypoint
  N3: AC_power_entry_/_power_strip.AC_to_12V_adapter_C, Adjustable_12V_adapter_C.AC_input, wp_18_0_50.waypoint, wp_19_1_51.waypoint
  N4: AC_power_entry_/_power_strip.AC_to_12V_adapter_D, Adjustable_12V_adapter_D.AC_input, wp_12_0_46.waypoint, wp_13_1_47.waypoint
  N5: AC_power_entry_/_power_strip.AC_to_Epson_printer_PSU, Epson_manufacturer_printer_PSU.AC_input, wp_3_0_40.waypoint, wp_4_1_41.waypoint
  N6: AC_power_entry_/_power_strip.AC_to_Raspberry_Pi_PSU, Raspberry_Pi_official_PSU.AC_input, wp_6_0_42.waypoint, wp_7_1_43.waypoint
  N7: AC_power_entry_/_power_strip.AC_to_LS108GP_adapter, LS108GP_manufacturer_power_adapter.AC_input, wp_0_0_38.waypoint, wp_1_1_39.waypoint
  N8: LS108GP_manufacturer_power_adapter.53.5V_DC_to_switch_only, TP-Link_LiteWave_LS108GP_8-port_PoE_switch.53.5V_DC_input_from_TP-Link_adapter, wp_21_0_52.waypoint, wp_22_1_53.waypoint
  N9: Epson_manufacturer_printer_PSU.Printer_DC_input_only, Epson_receipt_printer.Epson_PSU_input, wp_24_0_54.waypoint, wp_25_1_55.waypoint
  N10: Raspberry_Pi_official_PSU.Pi_power_input_only, Optional_Raspberry_Pi_master_controller_/_print_host.Official_Raspberry_Pi_PSU_input, wp_27_0_56.waypoint, wp_28_1_57.waypoint
  N11: Adjustable_12V_adapter_A.DC_negative, Adjustable_12V_adapter_D.DC_negative, Adjustable_12V_adapter_B.DC_negative, Adjustable_12V_adapter_C.DC_negative, Buck_#1_optional_5V_AUX.12V_input_negative, Buck_#1_optional_5V_AUX.5V_AUX_ground, Buck_#2_5V_LED.12V_input_negative, Buck_#2_5V_LED.5V_LED_ground, Buck_#3_5V_AUDIO_SERVO.12V_input_negative, Buck_#3_5V_AUDIO_SERVO.5V_AUDIO_SERVO_ground, COMMON_GND_distribution_terminal_block.COMMON_GND_tap_0, COMMON_GND_distribution_terminal_block.COMMON_GND_tap_1, COMMON_GND_distribution_terminal_block.COMMON_GND_tap_2, COMMON_GND_distribution_terminal_block.COMMON_GND_tap_3, COMMON_GND_distribution_terminal_block.COMMON_GND_tap_4, COMMON_GND_distribution_terminal_block.COMMON_GND_tap_5, COMMON_GND_distribution_terminal_block.COMMON_GND_tap_6, COMMON_GND_distribution_terminal_block.COMMON_GND_tap_7, COMMON_GND_distribution_terminal_block.COMMON_GND_tap_8, COMMON_GND_distribution_terminal_block.COMMON_GND_tap_9, COMMON_GND_distribution_terminal_block.COMMON_GND_tap_10, COMMON_GND_distribution_terminal_block.COMMON_GND_tap_11, COMMON_GND_distribution_terminal_block.COMMON_GND_tap_12, COMMON_GND_distribution_terminal_block.COMMON_GND_tap_13, COMMON_GND_distribution_terminal_block.COMMON_GND_tap_14, COMMON_GND_distribution_terminal_block.COMMON_GND_tap_15, Simon_ESP32_PoE_board.ESP32_GND_reference_to_COMMON_GND, Simon_local_accessory_terminal_block.Accessory_load_ground_to_COMMON_GND, Chop_ESP32_PoE_board.ESP32_GND_reference_to_COMMON_GND, Chop_local_accessory_terminal_block.Accessory_load_ground_to_COMMON_GND, Pan_ESP32_PoE_board.ESP32_GND_reference_to_COMMON_GND, Pan_local_accessory_terminal_block.Accessory_load_ground_to_COMMON_GND, Pot_ESP32_PoE_board.ESP32_GND_reference_to_COMMON_GND, Pot_local_accessory_terminal_block.Accessory_load_ground_to_COMMON_GND, Garnish_ESP32_PoE_board.ESP32_GND_reference_to_COMMON_GND, Garnish_local_accessory_terminal_block.Accessory_load_ground_to_COMMON_GND, wp_78_0_91.waypoint, wp_79_1_92.waypoint, wp_81_0_93.waypoint, wp_82_1_94.waypoint, wp_84_0_95.waypoint, wp_85_1_96.waypoint, wp_87_0_97.waypoint, wp_88_1_98.waypoint, wp_90_0_99.waypoint, wp_91_1_100.waypoint, wp_93_0_101.waypoint, wp_94_1_102.waypoint, wp_96_1_103.waypoint, wp_98_0_104.waypoint, wp_99_1_105.waypoint, wp_101_0_106.waypoint, wp_102_1_107.waypoint, wp_104_0_108.waypoint, wp_105_1_109.waypoint, wp_110_0_112.waypoint, wp_112_0_113.waypoint, wp_117_0_116.waypoint, wp_119_0_117.waypoint, wp_124_0_120.waypoint, wp_126_0_121.waypoint, wp_131_0_124.waypoint, wp_133_0_125.waypoint, wp_138_0_128.waypoint, wp_140_0_129.waypoint
  N12: Adjustable_12V_adapter_A.+12V_output, 12V_SHOW_/_12V_ACTUAL_LOADS_terminal_block.12V_SHOW_/_12V_ACTUAL_LOADS_tap_0, 12V_SHOW_/_12V_ACTUAL_LOADS_terminal_block.12V_SHOW_/_12V_ACTUAL_LOADS_tap_9, 12V_SHOW_/_12V_ACTUAL_LOADS_terminal_block.12V_SHOW_/_12V_ACTUAL_LOADS_tap_11, 12V_SHOW_/_12V_ACTUAL_LOADS_terminal_block.12V_SHOW_/_12V_ACTUAL_LOADS_tap_13, Simon_local_accessory_terminal_block.12V_SHOW_input_if_module_has_12V-rated_loads, Pan_local_accessory_terminal_block.12V_SHOW_input_if_module_has_12V-rated_loads, Pot_local_accessory_terminal_block.12V_SHOW_input_if_module_has_12V-rated_loads, wp_56_0_76.waypoint, wp_57_1_77.waypoint, wp_58_2_78.waypoint, wp_142_0_130.waypoint, wp_143_1_131.waypoint, wp_154_0_138.waypoint, wp_155_1_139.waypoint, wp_163_0_144.waypoint, wp_164_1_145.waypoint
  N13: Adjustable_12V_adapter_D.+12V_output, Buck_#1_optional_5V_AUX.12V_input_positive, wp_60_0_79.waypoint, wp_61_1_80.waypoint
  N14: Adjustable_12V_adapter_B.+12V_output, Buck_#2_5V_LED.12V_input_positive, wp_63_0_81.waypoint, wp_64_1_82.waypoint
  N15: Adjustable_12V_adapter_C.+12V_output, Buck_#3_5V_AUDIO_SERVO.12V_input_positive, wp_66_0_83.waypoint, wp_67_1_84.waypoint
  N16: TP-Link_LiteWave_LS108GP_8-port_PoE_switch.Port_1_PoE_to_Simon_ESP32, Simon_ESP32_PoE_board.Ethernet_+_PoE_input, wp_30_0_58.waypoint, wp_31_1_59.waypoint
  N17: TP-Link_LiteWave_LS108GP_8-port_PoE_switch.Port_2_PoE_to_Chopping_ESP32, Chop_ESP32_PoE_board.Ethernet_+_PoE_input, wp_33_0_60.waypoint, wp_34_1_61.waypoint
  N18: TP-Link_LiteWave_LS108GP_8-port_PoE_switch.Port_3_PoE_to_Pan_Motion_ESP32, Pan_ESP32_PoE_board.Ethernet_+_PoE_input, wp_36_0_62.waypoint, wp_37_1_63.waypoint
  N19: TP-Link_LiteWave_LS108GP_8-port_PoE_switch.Port_4_PoE_to_Pot_Temperature_ESP32, Pot_ESP32_PoE_board.Ethernet_+_PoE_input, wp_39_0_64.waypoint, wp_40_1_65.waypoint
  N20: TP-Link_LiteWave_LS108GP_8-port_PoE_switch.Port_5_PoE_to_Garnish_ESP32, Garnish_ESP32_PoE_board.Ethernet_+_PoE_input, wp_42_0_66.waypoint, wp_43_1_67.waypoint
  N21: TP-Link_LiteWave_LS108GP_8-port_PoE_switch.Port_6_Ethernet_to_Raspberry_Pi, Optional_Raspberry_Pi_master_controller_/_print_host.Ethernet_to_switch, wp_45_0_68.waypoint, wp_46_1_69.waypoint, wp_47_2_70.waypoint
  N22: TP-Link_LiteWave_LS108GP_8-port_PoE_switch.Port_7_Ethernet_to_Epson_printer, Epson_receipt_printer.Ethernet_to_switch, wp_49_0_71.waypoint, wp_50_1_72.waypoint, wp_51_2_73.waypoint
  N23: TP-Link_LiteWave_LS108GP_8-port_PoE_switch.Port_8_optional_router/DHCP_or_spare, Optional_router_/_DHCP_source.Ethernet_uplink_to_switch, wp_53_0_74.waypoint, wp_54_1_75.waypoint
  N24: Buck_#1_optional_5V_AUX.5V_AUX_positive, 5V_AUX_terminal_block.5V_AUX_tap_0, 5V_AUX_terminal_block.5V_AUX_tap_8, 5V_AUX_terminal_block.5V_AUX_tap_13, Chop_local_accessory_terminal_block.5V_AUX_input, Pot_local_accessory_terminal_block.5V_AUX_input, wp_69_0_85.waypoint, wp_70_1_86.waypoint, wp_151_0_136.waypoint, wp_152_1_137.waypoint, wp_169_0_148.waypoint, wp_170_1_149.waypoint
  N25: Buck_#2_5V_LED.5V_LED_positive, 5V_LED_terminal_block.5V_LED_tap_0, 5V_LED_terminal_block.5V_LED_tap_9, 5V_LED_terminal_block.5V_LED_tap_11, 5V_LED_terminal_block.5V_LED_tap_13, 5V_LED_terminal_block.5V_LED_tap_15, Simon_local_accessory_terminal_block.5V_LED_input, Pan_local_accessory_terminal_block.5V_LED_input, Pot_local_accessory_terminal_block.5V_LED_input, Garnish_local_accessory_terminal_block.5V_LED_input, wp_72_0_87.waypoint, wp_73_1_88.waypoint, wp_145_0_132.waypoint, wp_146_1_133.waypoint, wp_157_0_140.waypoint, wp_158_1_141.waypoint, wp_166_0_146.waypoint, wp_167_1_147.waypoint, wp_172_0_150.waypoint, wp_173_1_151.waypoint
  N26: Buck_#3_5V_AUDIO_SERVO.5V_AUDIO_SERVO_positive, 5V_AUDIO_SERVO_terminal_block.5V_AUDIO_SERVO_tap_0, 5V_AUDIO_SERVO_terminal_block.5V_AUDIO_SERVO_tap_9, 5V_AUDIO_SERVO_terminal_block.5V_AUDIO_SERVO_tap_11, 5V_AUDIO_SERVO_terminal_block.5V_AUDIO_SERVO_tap_15, Simon_local_accessory_terminal_block.5V_AUDIO_SERVO_input, Pan_local_accessory_terminal_block.5V_AUDIO_SERVO_input, Garnish_local_accessory_terminal_block.5V_AUDIO_SERVO_input, wp_75_0_89.waypoint, wp_76_1_90.waypoint, wp_148_0_134.waypoint, wp_149_1_135.waypoint, wp_160_0_142.waypoint, wp_161_1_143.waypoint, wp_175_0_152.waypoint, wp_176_1_153.waypoint
  N27: Simon_ESP32_PoE_board.GPIO/data/control_to_accessory_drivers, Simon_local_accessory_terminal_block.GPIO/data/control_from_ESP32, wp_107_0_110.waypoint, wp_108_1_111.waypoint
  N28: Chop_ESP32_PoE_board.GPIO/data/control_to_accessory_drivers, Chop_local_accessory_terminal_block.GPIO/data/control_from_ESP32, wp_114_0_114.waypoint, wp_115_1_115.waypoint
  N29: Pan_ESP32_PoE_board.GPIO/data/control_to_accessory_drivers, Pan_local_accessory_terminal_block.GPIO/data/control_from_ESP32, wp_121_0_118.waypoint, wp_122_1_119.waypoint
  N30: Pot_ESP32_PoE_board.GPIO/data/control_to_accessory_drivers, Pot_local_accessory_terminal_block.GPIO/data/control_from_ESP32, wp_128_0_122.waypoint, wp_129_1_123.waypoint
  N31: Garnish_ESP32_PoE_board.GPIO/data/control_to_accessory_drivers, Garnish_local_accessory_terminal_block.GPIO/data/control_from_ESP32, wp_135_0_126.waypoint, wp_136_1_127.waypoint
