# Fritzing sketch chef_station_master_power_network_editable (saved by Fritzing 1.0.3)

parts:
  Chef_Station_Master_Power_And_Network_Layout = Chef Station Master Power And Network Layout  # not connected
  Wire_color_legend = Wire color legend  # not connected
  AC_power_entry_/_power_strip = AC power entry / power strip
  LS108GP_manufacturer_power_adapter = LS108GP power adapter
  Epson_manufacturer_printer_PSU = Epson printer PSU
  Adjustable_12V_adapter_A = 12V Adapter A
  Adjustable_12V_adapter_D = 12V Adapter D
  Adjustable_12V_adapter_B = 12V Adapter B
  Adjustable_12V_adapter_C = 12V Adapter C
  TP-Link_LiteWave_LS108GP_8-port_PoE_switch = TP-Link LiteWave LS108GP PoE switch
  Optional_router_/_DHCP_source = Optional router / DHCP source
  Master_Controller_ESP32_PoE_board = Master Controller ESP32 PoE board
  Start_Game_button = Master Controller Start Game button
  Epson_receipt_printer = Epson TM-T20IV / TM-T20V-family receipt printer
  Buck_#1_optional_5V_AUX = Buck #1
  Buck_#2_5V_LED = Buck #2
  Buck_#3_5V_AUDIO_SERVO = Buck #3
  12V_SHOW_/_12V_ACTUAL_LOADS_terminal_block = 12V_SHOW / 12V ACTUAL LOADS
  5V_LED_terminal_block = 5V_LED
  5V_AUDIO_SERVO_terminal_block = 5V_AUDIO_SERVO
  5V_AUX_terminal_block = 5V_AUX
  COMMON_GND_distribution_terminal_block = COMMON_GND
  Simon_ESP32_PoE_board = Simon ESP32 PoE board
  Simon_local_accessory_terminal_block = Simon local accessory terminal block
  Chop_ESP32_PoE_board = Chopping ESP32 PoE board
  Chop_local_accessory_terminal_block = Chopping local accessory terminal block
  Pan_ESP32_PoE_board = Pan Motion ESP32 PoE board
  Pan_local_accessory_terminal_block = Pan Motion local accessory terminal block
  Pot_ESP32_PoE_board = Pot Temperature ESP32 PoE board
  Pot_local_accessory_terminal_block = Pot Temperature local accessory terminal block
  Garnish_ESP32_PoE_board = Garnish ESP32 PoE board
  Garnish_local_accessory_terminal_block = Garnish local accessory terminal block
  PoE_budget_table = PoE budget table  # not connected
  Power-source_table = Power-source table  # not connected
  Safety_and_separation_callouts = Safety and separation callouts  # not connected
  Grounding_rule = Grounding rule  # not connected
  Network_behavior = Network behavior  # not connected
  Setup_checklist_highlights = Setup checklist highlights  # not connected
  wp_0_0_38 = Wire waypoint
  wp_1_1_39 = Wire waypoint
  wp_3_0_40 = Wire waypoint
  wp_4_1_41 = Wire waypoint
  wp_6_0_42 = Wire waypoint
  wp_7_1_43 = Wire waypoint
  wp_9_0_44 = Wire waypoint
  wp_10_1_45 = Wire waypoint
  wp_12_0_46 = Wire waypoint
  wp_13_1_47 = Wire waypoint
  wp_15_0_48 = Wire waypoint
  wp_16_1_49 = Wire waypoint
  wp_18_0_50 = Wire waypoint
  wp_19_1_51 = Wire waypoint
  wp_21_0_52 = Wire waypoint
  wp_22_1_53 = Wire waypoint
  wp_24_0_54 = Wire waypoint
  wp_25_1_55 = Wire waypoint
  wp_27_0_56 = Wire waypoint
  wp_28_1_57 = Wire waypoint
  wp_30_0_58 = Wire waypoint
  wp_31_1_59 = Wire waypoint
  wp_33_0_60 = Wire waypoint
  wp_34_1_61 = Wire waypoint
  wp_36_0_62 = Wire waypoint
  wp_37_1_63 = Wire waypoint
  wp_39_0_64 = Wire waypoint
  wp_40_1_65 = Wire waypoint
  wp_41_2_66 = Wire waypoint
  wp_43_0_67 = Wire waypoint
  wp_44_1_68 = Wire waypoint
  wp_45_2_69 = Wire waypoint
  wp_47_0_70 = Wire waypoint
  wp_48_1_71 = Wire waypoint
  wp_50_0_72 = Wire waypoint
  wp_51_1_73 = Wire waypoint
  wp_53_0_74 = Wire waypoint
  wp_55_0_75 = Wire waypoint
  wp_56_1_76 = Wire waypoint
  wp_58_0_77 = Wire waypoint
  wp_59_1_78 = Wire waypoint
  wp_60_2_79 = Wire waypoint
  wp_62_0_80 = Wire waypoint
  wp_63_1_81 = Wire waypoint
  wp_65_0_82 = Wire waypoint
  wp_66_1_83 = Wire waypoint
  wp_68_0_84 = Wire waypoint
  wp_69_1_85 = Wire waypoint
  wp_71_0_86 = Wire waypoint
  wp_72_1_87 = Wire waypoint
  wp_74_0_88 = Wire waypoint
  wp_75_1_89 = Wire waypoint
  wp_77_0_90 = Wire waypoint
  wp_78_1_91 = Wire waypoint
  wp_80_0_92 = Wire waypoint
  wp_81_1_93 = Wire waypoint
  wp_83_0_94 = Wire waypoint
  wp_84_1_95 = Wire waypoint
  wp_86_0_96 = Wire waypoint
  wp_87_1_97 = Wire waypoint
  wp_89_0_98 = Wire waypoint
  wp_90_1_99 = Wire waypoint
  wp_92_0_100 = Wire waypoint
  wp_93_1_101 = Wire waypoint
  wp_95_0_102 = Wire waypoint
  wp_96_1_103 = Wire waypoint
  wp_98_1_104 = Wire waypoint
  wp_100_0_105 = Wire waypoint
  wp_101_1_106 = Wire waypoint
  wp_103_0_107 = Wire waypoint
  wp_104_1_108 = Wire waypoint
  wp_106_0_109 = Wire waypoint
  wp_107_1_110 = Wire waypoint
  wp_109_0_111 = Wire waypoint
  wp_110_1_112 = Wire waypoint
  wp_112_0_113 = Wire waypoint
  wp_114_0_114 = Wire waypoint
  wp_116_0_115 = Wire waypoint
  wp_117_1_116 = Wire waypoint
  wp_119_0_117 = Wire waypoint
  wp_121_0_118 = Wire waypoint
  wp_123_0_119 = Wire waypoint
  wp_124_1_120 = Wire waypoint
  wp_126_0_121 = Wire waypoint
  wp_128_0_122 = Wire waypoint
  wp_130_0_123 = Wire waypoint
  wp_131_1_124 = Wire waypoint
  wp_133_0_125 = Wire waypoint
  wp_135_0_126 = Wire waypoint
  wp_137_0_127 = Wire waypoint
  wp_138_1_128 = Wire waypoint
  wp_140_0_129 = Wire waypoint
  wp_142_0_130 = Wire waypoint
  wp_144_0_131 = Wire waypoint
  wp_145_1_132 = Wire waypoint
  wp_147_0_133 = Wire waypoint
  wp_148_1_134 = Wire waypoint
  wp_150_0_135 = Wire waypoint
  wp_151_1_136 = Wire waypoint
  wp_153_0_137 = Wire waypoint
  wp_154_1_138 = Wire waypoint
  wp_156_0_139 = Wire waypoint
  wp_157_1_140 = Wire waypoint
  wp_159_0_141 = Wire waypoint
  wp_160_1_142 = Wire waypoint
  wp_162_0_143 = Wire waypoint
  wp_163_1_144 = Wire waypoint
  wp_165_0_145 = Wire waypoint
  wp_166_1_146 = Wire waypoint
  wp_168_0_147 = Wire waypoint
  wp_169_1_148 = Wire waypoint
  wp_171_0_149 = Wire waypoint
  wp_172_1_150 = Wire waypoint
  wp_174_0_151 = Wire waypoint
  wp_175_1_152 = Wire waypoint
  wp_177_0_153 = Wire waypoint
  wp_178_1_154 = Wire waypoint

nets:
  N1: AC_power_entry_/_power_strip.AC_to_12V_adapter_A, Adjustable_12V_adapter_A.AC_input, wp_6_0_42.waypoint, wp_7_1_43.waypoint
  N2: AC_power_entry_/_power_strip.AC_to_12V_adapter_B, Adjustable_12V_adapter_B.AC_input, wp_12_0_46.waypoint, wp_13_1_47.waypoint
  N3: AC_power_entry_/_power_strip.AC_to_12V_adapter_C, Adjustable_12V_adapter_C.AC_input, wp_15_0_48.waypoint, wp_16_1_49.waypoint
  N4: AC_power_entry_/_power_strip.AC_to_12V_adapter_D, Adjustable_12V_adapter_D.AC_input, wp_9_0_44.waypoint, wp_10_1_45.waypoint
  N5: AC_power_entry_/_power_strip.AC_to_Epson_printer_PSU, Epson_manufacturer_printer_PSU.AC_input, wp_3_0_40.waypoint, wp_4_1_41.waypoint
  N6: AC_power_entry_/_power_strip.AC_to_LS108GP_adapter, LS108GP_manufacturer_power_adapter.AC_input, wp_0_0_38.waypoint, wp_1_1_39.waypoint
  N7: LS108GP_manufacturer_power_adapter.53.5V_DC_to_switch_only, TP-Link_LiteWave_LS108GP_8-port_PoE_switch.53.5V_DC_input_from_TP-Link_adapter, wp_18_0_50.waypoint, wp_19_1_51.waypoint
  N8: Epson_manufacturer_printer_PSU.Printer_DC_input_only, Epson_receipt_printer.Epson_PSU_input, wp_21_0_52.waypoint, wp_22_1_53.waypoint
  N9: Adjustable_12V_adapter_A.DC_negative, Adjustable_12V_adapter_D.DC_negative, Adjustable_12V_adapter_B.DC_negative, Adjustable_12V_adapter_C.DC_negative, Master_Controller_ESP32_PoE_board.Master_ESP32_GND_reference_to_COMMON_GND, Master_Controller_ESP32_PoE_board.GND_pin_for_Start_Game_button, Start_Game_button.Start_button_ground, Buck_#1_optional_5V_AUX.12V_input_negative, Buck_#1_optional_5V_AUX.5V_AUX_ground, Buck_#2_5V_LED.12V_input_negative, Buck_#2_5V_LED.5V_LED_ground, Buck_#3_5V_AUDIO_SERVO.12V_input_negative, Buck_#3_5V_AUDIO_SERVO.5V_AUDIO_SERVO_ground, COMMON_GND_distribution_terminal_block.COMMON_GND_tap_0, COMMON_GND_distribution_terminal_block.COMMON_GND_tap_1, COMMON_GND_distribution_terminal_block.COMMON_GND_tap_2, COMMON_GND_distribution_terminal_block.COMMON_GND_tap_3, COMMON_GND_distribution_terminal_block.COMMON_GND_tap_4, COMMON_GND_distribution_terminal_block.COMMON_GND_tap_5, COMMON_GND_distribution_terminal_block.COMMON_GND_tap_6, COMMON_GND_distribution_terminal_block.COMMON_GND_tap_7, COMMON_GND_distribution_terminal_block.COMMON_GND_tap_8, COMMON_GND_distribution_terminal_block.COMMON_GND_tap_9, COMMON_GND_distribution_terminal_block.COMMON_GND_tap_10, COMMON_GND_distribution_terminal_block.COMMON_GND_tap_11, COMMON_GND_distribution_terminal_block.COMMON_GND_tap_12, COMMON_GND_distribution_terminal_block.COMMON_GND_tap_13, COMMON_GND_distribution_terminal_block.COMMON_GND_tap_14, COMMON_GND_distribution_terminal_block.COMMON_GND_tap_15, COMMON_GND_distribution_terminal_block.COMMON_GND_tap_16, Simon_ESP32_PoE_board.ESP32_GND_reference_to_COMMON_GND, Simon_local_accessory_terminal_block.Accessory_load_ground_to_COMMON_GND, Chop_ESP32_PoE_board.ESP32_GND_reference_to_COMMON_GND, Chop_local_accessory_terminal_block.Accessory_load_ground_to_COMMON_GND, Pan_ESP32_PoE_board.ESP32_GND_reference_to_COMMON_GND, Pan_local_accessory_terminal_block.Accessory_load_ground_to_COMMON_GND, Pot_ESP32_PoE_board.ESP32_GND_reference_to_COMMON_GND, Pot_local_accessory_terminal_block.Accessory_load_ground_to_COMMON_GND, Garnish_ESP32_PoE_board.ESP32_GND_reference_to_COMMON_GND, Garnish_local_accessory_terminal_block.Accessory_load_ground_to_COMMON_GND, wp_53_0_74.waypoint, wp_55_0_75.waypoint, wp_56_1_76.waypoint, wp_80_0_92.waypoint, wp_81_1_93.waypoint, wp_83_0_94.waypoint, wp_84_1_95.waypoint, wp_86_0_96.waypoint, wp_87_1_97.waypoint, wp_89_0_98.waypoint, wp_90_1_99.waypoint, wp_92_0_100.waypoint, wp_93_1_101.waypoint, wp_95_0_102.waypoint, wp_96_1_103.waypoint, wp_98_1_104.waypoint, wp_100_0_105.waypoint, wp_101_1_106.waypoint, wp_103_0_107.waypoint, wp_104_1_108.waypoint, wp_106_0_109.waypoint, wp_107_1_110.waypoint, wp_112_0_113.waypoint, wp_114_0_114.waypoint, wp_119_0_117.waypoint, wp_121_0_118.waypoint, wp_126_0_121.waypoint, wp_128_0_122.waypoint, wp_133_0_125.waypoint, wp_135_0_126.waypoint, wp_140_0_129.waypoint, wp_142_0_130.waypoint
  N10: Adjustable_12V_adapter_A.+12V_output, 12V_SHOW_/_12V_ACTUAL_LOADS_terminal_block.12V_SHOW_/_12V_ACTUAL_LOADS_tap_0, 12V_SHOW_/_12V_ACTUAL_LOADS_terminal_block.12V_SHOW_/_12V_ACTUAL_LOADS_tap_9, 12V_SHOW_/_12V_ACTUAL_LOADS_terminal_block.12V_SHOW_/_12V_ACTUAL_LOADS_tap_11, 12V_SHOW_/_12V_ACTUAL_LOADS_terminal_block.12V_SHOW_/_12V_ACTUAL_LOADS_tap_13, Simon_local_accessory_terminal_block.12V_SHOW_input_if_module_has_12V-rated_loads, Pan_local_accessory_terminal_block.12V_SHOW_input_if_module_has_12V-rated_loads, Pot_local_accessory_terminal_block.12V_SHOW_input_if_module_has_12V-rated_loads, wp_58_0_77.waypoint, wp_59_1_78.waypoint, wp_60_2_79.waypoint, wp_144_0_131.waypoint, wp_145_1_132.waypoint, wp_156_0_139.waypoint, wp_157_1_140.waypoint, wp_165_0_145.waypoint, wp_166_1_146.waypoint
  N11: Adjustable_12V_adapter_D.+12V_output, Buck_#1_optional_5V_AUX.12V_input_positive, wp_62_0_80.waypoint, wp_63_1_81.waypoint
  N12: Adjustable_12V_adapter_B.+12V_output, Buck_#2_5V_LED.12V_input_positive, wp_65_0_82.waypoint, wp_66_1_83.waypoint
  N13: Adjustable_12V_adapter_C.+12V_output, Buck_#3_5V_AUDIO_SERVO.12V_input_positive, wp_68_0_84.waypoint, wp_69_1_85.waypoint
  N14: TP-Link_LiteWave_LS108GP_8-port_PoE_switch.Port_1_PoE_to_Simon_ESP32, Simon_ESP32_PoE_board.Ethernet_+_PoE_input, wp_24_0_54.waypoint, wp_25_1_55.waypoint
  N15: TP-Link_LiteWave_LS108GP_8-port_PoE_switch.Port_2_PoE_to_Chopping_ESP32, Chop_ESP32_PoE_board.Ethernet_+_PoE_input, wp_27_0_56.waypoint, wp_28_1_57.waypoint
  N16: TP-Link_LiteWave_LS108GP_8-port_PoE_switch.Port_3_PoE_to_Pan_Motion_ESP32, Pan_ESP32_PoE_board.Ethernet_+_PoE_input, wp_30_0_58.waypoint, wp_31_1_59.waypoint
  N17: TP-Link_LiteWave_LS108GP_8-port_PoE_switch.Port_4_PoE_to_Pot_Temperature_ESP32, Pot_ESP32_PoE_board.Ethernet_+_PoE_input, wp_33_0_60.waypoint, wp_34_1_61.waypoint
  N18: TP-Link_LiteWave_LS108GP_8-port_PoE_switch.Port_5_PoE_to_Garnish_ESP32, Garnish_ESP32_PoE_board.Ethernet_+_PoE_input, wp_36_0_62.waypoint, wp_37_1_63.waypoint
  N19: TP-Link_LiteWave_LS108GP_8-port_PoE_switch.Port_6_PoE_to_Master_Controller_ESP32, Master_Controller_ESP32_PoE_board.Ethernet_+_PoE_input, wp_39_0_64.waypoint, wp_40_1_65.waypoint, wp_41_2_66.waypoint
  N20: TP-Link_LiteWave_LS108GP_8-port_PoE_switch.Port_7_Ethernet_to_Epson_printer, Epson_receipt_printer.Ethernet_to_switch, wp_43_0_67.waypoint, wp_44_1_68.waypoint, wp_45_2_69.waypoint
  N21: TP-Link_LiteWave_LS108GP_8-port_PoE_switch.Port_8_optional_router/DHCP_or_spare, Optional_router_/_DHCP_source.Ethernet_uplink_to_switch, wp_47_0_70.waypoint, wp_48_1_71.waypoint
  N22: Master_Controller_ESP32_PoE_board.GPIO5_Start_Game_button_input, Start_Game_button.Start_button_signal_to_GPIO5, wp_50_0_72.waypoint, wp_51_1_73.waypoint
  N23: Buck_#1_optional_5V_AUX.5V_AUX_positive, 5V_AUX_terminal_block.5V_AUX_tap_0, 5V_AUX_terminal_block.5V_AUX_tap_8, 5V_AUX_terminal_block.5V_AUX_tap_13, Chop_local_accessory_terminal_block.5V_AUX_input, Pot_local_accessory_terminal_block.5V_AUX_input, wp_71_0_86.waypoint, wp_72_1_87.waypoint, wp_153_0_137.waypoint, wp_154_1_138.waypoint, wp_171_0_149.waypoint, wp_172_1_150.waypoint
  N24: Buck_#2_5V_LED.5V_LED_positive, 5V_LED_terminal_block.5V_LED_tap_0, 5V_LED_terminal_block.5V_LED_tap_9, 5V_LED_terminal_block.5V_LED_tap_11, 5V_LED_terminal_block.5V_LED_tap_13, 5V_LED_terminal_block.5V_LED_tap_15, Simon_local_accessory_terminal_block.5V_LED_input, Pan_local_accessory_terminal_block.5V_LED_input, Pot_local_accessory_terminal_block.5V_LED_input, Garnish_local_accessory_terminal_block.5V_LED_input, wp_74_0_88.waypoint, wp_75_1_89.waypoint, wp_147_0_133.waypoint, wp_148_1_134.waypoint, wp_159_0_141.waypoint, wp_160_1_142.waypoint, wp_168_0_147.waypoint, wp_169_1_148.waypoint, wp_174_0_151.waypoint, wp_175_1_152.waypoint
  N25: Buck_#3_5V_AUDIO_SERVO.5V_AUDIO_SERVO_positive, 5V_AUDIO_SERVO_terminal_block.5V_AUDIO_SERVO_tap_0, 5V_AUDIO_SERVO_terminal_block.5V_AUDIO_SERVO_tap_9, 5V_AUDIO_SERVO_terminal_block.5V_AUDIO_SERVO_tap_11, 5V_AUDIO_SERVO_terminal_block.5V_AUDIO_SERVO_tap_15, Simon_local_accessory_terminal_block.5V_AUDIO_SERVO_input, Pan_local_accessory_terminal_block.5V_AUDIO_SERVO_input, Garnish_local_accessory_terminal_block.5V_AUDIO_SERVO_input, wp_77_0_90.waypoint, wp_78_1_91.waypoint, wp_150_0_135.waypoint, wp_151_1_136.waypoint, wp_162_0_143.waypoint, wp_163_1_144.waypoint, wp_177_0_153.waypoint, wp_178_1_154.waypoint
  N26: Simon_ESP32_PoE_board.GPIO/data/control_to_accessory_drivers, Simon_local_accessory_terminal_block.GPIO/data/control_from_ESP32, wp_109_0_111.waypoint, wp_110_1_112.waypoint
  N27: Chop_ESP32_PoE_board.GPIO/data/control_to_accessory_drivers, Chop_local_accessory_terminal_block.GPIO/data/control_from_ESP32, wp_116_0_115.waypoint, wp_117_1_116.waypoint
  N28: Pan_ESP32_PoE_board.GPIO/data/control_to_accessory_drivers, Pan_local_accessory_terminal_block.GPIO/data/control_from_ESP32, wp_123_0_119.waypoint, wp_124_1_120.waypoint
  N29: Pot_ESP32_PoE_board.GPIO/data/control_to_accessory_drivers, Pot_local_accessory_terminal_block.GPIO/data/control_from_ESP32, wp_130_0_123.waypoint, wp_131_1_124.waypoint
  N30: Garnish_ESP32_PoE_board.GPIO/data/control_to_accessory_drivers, Garnish_local_accessory_terminal_block.GPIO/data/control_from_ESP32, wp_137_0_127.waypoint, wp_138_1_128.waypoint
