# Fritzing sketch chef_station_pan_motion_cooktop_editable (saved by Fritzing 1.0.3)

parts:
  Chef_Station_"Pan_Motion_/_Cooktop"_wiring = Chef Station "Pan Motion / Cooktop" wiring  # not connected
  Pin_assignment_summary = Pin assignment summary  # not connected
  Controller_note = Controller note  # not connected
  Power_callouts = Power callouts  # not connected
  Rail_labels = Rail labels  # not connected
  Hall_sensing_notes = Hall sensing notes  # not connected
  Minimum_viable_Hall_layout = Minimum viable Hall layout  # not connected
  Firmware_behavior = Firmware behavior  # not connected
  DFPlayer_audio_behavior = DFPlayer audio behavior  # not connected
  Speaker_connection = Speaker connection  # not connected
  RGB_coil_note = RGB coil note  # not connected
  Waveshare_ESP32-P4-POE-ETH_/_ESP32-P4-POE-ETH-NH = Waveshare ESP32-P4-POE-ETH / ESP32-P4-POE-ETH-NH
  Manhattan_breadboard_and_rails_area = Breadboard and power rails area  # not connected
  5V_LED_input_from_master_power_rails = Named 5V accessory rail input
  5V_AUDIO_SERVO_input_from_master_power_rails = Named 5V accessory rail input
  5V_LED_local_rail = 5V_LED rail
  ESP32_3_3V_Hall_rail = ESP32 3.3V Hall rail
  5V_AUDIO_SERVO_local_rail = 5V_AUDIO_SERVO rail
  COMMON_GND_rail = COMMON_GND rail
  R3_330_ohm_LED_data_resistor_(330-470_ohm_OK) = 330-470 ohm LED data resistor [Resistance="330 ohm"]
  R1_1k_HALL_1_AO_series_resistor = 1k series resistor [Resistance=1k]
  R2_1k_HALL_2_AO_series_resistor = 1k series resistor [Resistance=1k]
  R4_1k_ESP32_TX_to_DFPlayer_RX = 1k series resistor [Resistance=1k]
  Series_resistors = Series resistors  # not connected
  Fake_cooktop_and_pan_physical_layout = Cooktop physical layout  # not connected
  Cooktop_coil_RGB_strip_+5V_/_DIN_/_GND = Cooktop coil RGB strip: +5V / DIN / GND
  HALL_1_analog_Hall_sensor_left_of_burner_center = HALL 1 analog linear Hall sensor
  HALL_2_analog_Hall_sensor_right_of_burner_center = HALL 2 analog linear Hall sensor
  C1_0_1uF_near_HALL_1 = 0.1uF Hall decoupling capacitor [Capacitance=0.1uF]
  C2_0_1uF_near_HALL_2 = 0.1uF Hall decoupling capacitor [Capacitance=0.1uF]
  C3_1000uF_electrolytic_near_RGB_strip = Electrolytic Capacitor [Capacitance=1000uF package=THT]
  DFPlayer_Mini_with_microSD_card = DFRobot DFPlayer Mini
  C4_470uF-1000uF_electrolytic_near_DFPlayer = Electrolytic Capacitor [Capacitance=470uF-1000uF package=THT]
  4_or_8_ohm_speaker_2-3W = Loudspeaker
  DFPlayer_Mini = DFPlayer Mini  # not connected
  wp_0_0_35 = Wire waypoint
  wp_1_1_36 = Wire waypoint
  wp_3_0_37 = Wire waypoint
  wp_4_1_38 = Wire waypoint
  wp_6_0_39 = Wire waypoint
  wp_7_1_40 = Wire waypoint
  wp_9_0_41 = Wire waypoint
  wp_10_1_42 = Wire waypoint
  wp_12_0_43 = Wire waypoint
  wp_13_1_44 = Wire waypoint
  wp_15_0_45 = Wire waypoint
  wp_16_1_46 = Wire waypoint
  wp_18_0_47 = Wire waypoint
  wp_19_1_48 = Wire waypoint
  wp_21_0_49 = Wire waypoint
  wp_22_1_50 = Wire waypoint
  wp_24_0_51 = Wire waypoint
  wp_25_1_52 = Wire waypoint
  wp_27_0_53 = Wire waypoint
  wp_28_1_54 = Wire waypoint
  wp_30_0_55 = Wire waypoint
  wp_32_0_56 = Wire waypoint
  wp_34_0_57 = Wire waypoint
  wp_36_0_58 = Wire waypoint
  wp_38_1_59 = Wire waypoint
  wp_40_0_60 = Wire waypoint
  wp_41_1_61 = Wire waypoint
  wp_43_0_62 = Wire waypoint
  wp_44_1_63 = Wire waypoint
  wp_46_0_64 = Wire waypoint
  wp_47_1_65 = Wire waypoint
  wp_49_0_66 = Wire waypoint
  wp_50_1_67 = Wire waypoint
  wp_52_0_68 = Wire waypoint
  wp_53_1_69 = Wire waypoint
  wp_55_0_70 = Wire waypoint
  wp_56_1_71 = Wire waypoint
  wp_58_0_72 = Wire waypoint
  wp_59_1_73 = Wire waypoint
  wp_61_0_74 = Wire waypoint
  wp_62_1_75 = Wire waypoint
  wp_64_0_76 = Wire waypoint
  wp_65_1_77 = Wire waypoint
  wp_67_0_78 = Wire waypoint
  wp_68_1_79 = Wire waypoint
  wp_70_0_80 = Wire waypoint
  wp_71_1_81 = Wire waypoint
  wp_73_0_82 = Wire waypoint
  wp_74_1_83 = Wire waypoint
  wp_76_0_84 = Wire waypoint
  wp_77_1_85 = Wire waypoint
  wp_79_0_86 = Wire waypoint
  wp_80_1_87 = Wire waypoint
  wp_82_1_88 = Wire waypoint
  wp_84_0_89 = Wire waypoint
  wp_85_1_90 = Wire waypoint
  wp_87_0_91 = Wire waypoint
  wp_88_1_92 = Wire waypoint
  wp_90_0_93 = Wire waypoint
  wp_91_1_94 = Wire waypoint

nets:
  N1: Waveshare_ESP32-P4-POE-ETH_/_ESP32-P4-POE-ETH-NH.3V3_Hall_rail, ESP32_3_3V_Hall_rail.ESP32_3.3V_Hall_rail_tap_0, ESP32_3_3V_Hall_rail.ESP32_3.3V_Hall_rail_tap_10, ESP32_3_3V_Hall_rail.ESP32_3.3V_Hall_rail_tap_14, HALL_1_analog_Hall_sensor_left_of_burner_center.3.3V_VCC, HALL_2_analog_Hall_sensor_right_of_burner_center.3.3V_VCC, C1_0_1uF_near_HALL_1.3.3V_side, C2_0_1uF_near_HALL_2.3.3V_side, wp_15_0_45.waypoint, wp_16_1_46.waypoint, wp_18_0_47.waypoint, wp_19_1_48.waypoint, wp_24_0_51.waypoint, wp_25_1_52.waypoint, wp_30_0_55.waypoint, wp_34_0_57.waypoint
  GND: Waveshare_ESP32-P4-POE-ETH_/_ESP32-P4-POE-ETH-NH.GND, 5V_LED_input_from_master_power_rails.COMMON_GND, 5V_AUDIO_SERVO_input_from_master_power_rails.COMMON_GND, COMMON_GND_rail.COMMON_GND_rail_tap_0, COMMON_GND_rail.COMMON_GND_rail_tap_1, COMMON_GND_rail.COMMON_GND_rail_tap_2, COMMON_GND_rail.COMMON_GND_rail_tap_10, COMMON_GND_rail.COMMON_GND_rail_tap_14, COMMON_GND_rail.COMMON_GND_rail_tap_15, COMMON_GND_rail.COMMON_GND_rail_tap_17, Cooktop_coil_RGB_strip_+5V_/_DIN_/_GND.LED_strip_GND, HALL_1_analog_Hall_sensor_left_of_burner_center.GND, HALL_2_analog_Hall_sensor_right_of_burner_center.GND, C1_0_1uF_near_HALL_1.GND_side, C2_0_1uF_near_HALL_2.GND_side, C3_1000uF_electrolytic_near_RGB_strip.-, DFPlayer_Mini_with_microSD_card.GND-1, C4_470uF-1000uF_electrolytic_near_DFPlayer.-, wp_3_0_37.waypoint, wp_4_1_38.waypoint, wp_9_0_41.waypoint, wp_10_1_42.waypoint, wp_12_0_43.waypoint, wp_13_1_44.waypoint, wp_21_0_49.waypoint, wp_22_1_50.waypoint, wp_27_0_53.waypoint, wp_28_1_54.waypoint, wp_32_0_56.waypoint, wp_36_0_58.waypoint, wp_52_0_68.waypoint, wp_53_1_69.waypoint, wp_64_0_76.waypoint, wp_65_1_77.waypoint, wp_70_0_80.waypoint, wp_71_1_81.waypoint, wp_76_0_84.waypoint, wp_77_1_85.waypoint
  N2: Waveshare_ESP32-P4-POE-ETH_/_ESP32-P4-POE-ETH-NH.GPIO27_/_DF_TX, DFPlayer_Mini_with_microSD_card.TX, wp_84_0_89.waypoint, wp_85_1_90.waypoint
  N3: Waveshare_ESP32-P4-POE-ETH_/_ESP32-P4-POE-ETH-NH.GPIO26_/_DF_RX, R4_1k_ESP32_TX_to_DFPlayer_RX.lead_A, wp_79_0_86.waypoint, wp_80_1_87.waypoint
  N4: Waveshare_ESP32-P4-POE-ETH_/_ESP32-P4-POE-ETH-NH.GPIO23_/_LED_DATA, R3_330_ohm_LED_data_resistor_(330-470_ohm_OK).lead_A, wp_55_0_70.waypoint, wp_56_1_71.waypoint
  N5: Waveshare_ESP32-P4-POE-ETH_/_ESP32-P4-POE-ETH-NH.GPIO20_/_HALL1_AO, R1_1k_HALL_1_AO_series_resistor.lead_A, wp_40_0_60.waypoint, wp_41_1_61.waypoint
  N6: Waveshare_ESP32-P4-POE-ETH_/_ESP32-P4-POE-ETH-NH.GPIO21_/_HALL2_AO, R2_1k_HALL_2_AO_series_resistor.lead_A, wp_46_0_64.waypoint, wp_47_1_65.waypoint
  N7: 5V_LED_input_from_master_power_rails.+5V_rail_input, 5V_LED_local_rail.5V_LED_rail_tap_0, 5V_LED_local_rail.5V_LED_rail_tap_17, Cooktop_coil_RGB_strip_+5V_/_DIN_/_GND.LED_strip_+5V, C3_1000uF_electrolytic_near_RGB_strip.+, wp_0_0_35.waypoint, wp_1_1_36.waypoint, wp_49_0_66.waypoint, wp_50_1_67.waypoint, wp_61_0_74.waypoint, wp_62_1_75.waypoint
  N8: 5V_AUDIO_SERVO_input_from_master_power_rails.+5V_rail_input, 5V_AUDIO_SERVO_local_rail.5V_AUDIO_SERVO_rail_tap_0, 5V_AUDIO_SERVO_local_rail.5V_AUDIO_SERVO_rail_tap_15, DFPlayer_Mini_with_microSD_card.VCC, C4_470uF-1000uF_electrolytic_near_DFPlayer.+, wp_6_0_39.waypoint, wp_7_1_40.waypoint, wp_67_0_78.waypoint, wp_68_1_79.waypoint, wp_73_0_82.waypoint, wp_74_1_83.waypoint
  N9: R3_330_ohm_LED_data_resistor_(330-470_ohm_OK).lead_B, Cooktop_coil_RGB_strip_+5V_/_DIN_/_GND.LED_strip_DIN, wp_58_0_72.waypoint, wp_59_1_73.waypoint
  N10: R1_1k_HALL_1_AO_series_resistor.lead_B, HALL_1_analog_Hall_sensor_left_of_burner_center.AO_analog_output, wp_38_1_59.waypoint
  N11: R2_1k_HALL_2_AO_series_resistor.lead_B, HALL_2_analog_Hall_sensor_right_of_burner_center.AO_analog_output, wp_43_0_62.waypoint, wp_44_1_63.waypoint
  N12: R4_1k_ESP32_TX_to_DFPlayer_RX.lead_B, DFPlayer_Mini_with_microSD_card.RX, wp_82_1_88.waypoint
  N13: DFPlayer_Mini_with_microSD_card.SPK_1, 4_or_8_ohm_speaker_2-3W.pin2, wp_87_0_91.waypoint, wp_88_1_92.waypoint
  N14: DFPlayer_Mini_with_microSD_card.SPK_2, 4_or_8_ohm_speaker_2-3W.pin1, wp_90_0_93.waypoint, wp_91_1_94.waypoint
