# Fritzing sketch chef_station_pot_temperature_heat_balance_editable (saved by Fritzing 1.0.3)

parts:
  Chef_Station_"Pot_Temperature_/_Heat_Balance"_wiring = Chef Station "Pot Temperature / Heat Balance" wiring  # not connected
  Pin_assignment_summary = Pin assignment summary  # not connected
  Controller_note = Controller note  # not connected
  Power_callouts = Power callouts  # not connected
  Encoder_notes = Encoder notes  # not connected
  LED_behavior_callouts = LED behavior callouts  # not connected
  Game_logic_side_panel = Game logic side panel  # not connected
  LED_data_protection = LED data protection  # not connected
  1000uF_capacitor = 1000uF capacitor  # not connected
  Waveshare_ESP32-P4-POE-ETH_/_ESP32-P4-POE-ETH-NH = Waveshare ESP32-P4-POE-ETH / ESP32-P4-POE-ETH-NH
  Manhattan_breadboard_and_rails_area = Breadboard and power rails area  # not connected
  5V_LED_input_from_master_power_rails = 5V_LED rail input from master power distribution
  5V_LED_local_rail = 5V_LED rail
  ESP32_3_3V_optional_encoder_rail = ESP32 3.3V encoder rail
  COMMON_GND_rail = COMMON_GND rail
  R1_330-470_ohm_cooktop_coil_data_resistor = 330-470 ohm LED data resistor [Resistance="330-470 ohm"]
  R2_330-470_ohm_pot_temperature_data_resistor = 330-470 ohm LED data resistor [Resistance="330-470 ohm"]
  Rotary_encoder_/_KY-040_heat_control = Rotary encoder with optional KY-040 module VCC
  Cooktop_coil_RGB_strip_+5V_/_DIN_/_GND = Red/orange cooktop heat coil RGB strip
  Pot_temperature_indicator_strip/ring_+5V_/_DIN_/_GND = Pot temperature LED strip or ring
  C1_1000uF_electrolytic_near_LED_power_input = Electrolytic Capacitor [Capacitance=1000uF package=THT]
  wp_0_0_21 = Wire waypoint
  wp_1_1_22 = Wire waypoint
  wp_3_0_23 = Wire waypoint
  wp_4_1_24 = Wire waypoint
  wp_5_2_25 = Wire waypoint
  wp_7_0_26 = Wire waypoint
  wp_8_1_27 = Wire waypoint
  wp_10_0_28 = Wire waypoint
  wp_11_1_29 = Wire waypoint
  wp_13_0_30 = Wire waypoint
  wp_14_1_31 = Wire waypoint
  wp_16_0_32 = Wire waypoint
  wp_17_1_33 = Wire waypoint
  wp_19_0_34 = Wire waypoint
  wp_20_1_35 = Wire waypoint
  wp_22_0_36 = Wire waypoint
  wp_23_1_37 = Wire waypoint
  wp_25_0_38 = Wire waypoint
  wp_26_1_39 = Wire waypoint
  wp_28_0_40 = Wire waypoint
  wp_29_1_41 = Wire waypoint
  wp_31_0_42 = Wire waypoint
  wp_32_1_43 = Wire waypoint
  wp_34_0_44 = Wire waypoint
  wp_35_1_45 = Wire waypoint
  wp_37_0_46 = Wire waypoint
  wp_38_1_47 = Wire waypoint
  wp_39_2_48 = Wire waypoint
  wp_40_3_49 = Wire waypoint
  wp_42_0_50 = Wire waypoint
  wp_43_1_51 = Wire waypoint
  wp_45_0_52 = Wire waypoint
  wp_46_1_53 = Wire waypoint
  wp_48_0_54 = Wire waypoint
  wp_49_1_55 = Wire waypoint
  wp_51_0_56 = Wire waypoint
  wp_52_1_57 = Wire waypoint
  wp_54_0_58 = Wire waypoint
  wp_55_1_59 = Wire waypoint
  wp_57_0_60 = Wire waypoint
  wp_58_1_61 = Wire waypoint

nets:
  N1: Waveshare_ESP32-P4-POE-ETH_/_ESP32-P4-POE-ETH-NH.3V3, ESP32_3_3V_optional_encoder_rail.ESP32_3.3V_encoder_rail_tap_0, ESP32_3_3V_optional_encoder_rail.ESP32_3.3V_encoder_rail_tap_5, Rotary_encoder_/_KY-040_heat_control.VCC_3.3V, wp_10_0_28.waypoint, wp_11_1_29.waypoint, wp_45_0_52.waypoint, wp_46_1_53.waypoint
  GND: Waveshare_ESP32-P4-POE-ETH_/_ESP32-P4-POE-ETH-NH.GND, 5V_LED_input_from_master_power_rails.COMMON_GND, COMMON_GND_rail.COMMON_GND_rail_tap_0, COMMON_GND_rail.COMMON_GND_rail_tap_1, COMMON_GND_rail.COMMON_GND_rail_tap_5, COMMON_GND_rail.COMMON_GND_rail_tap_18, COMMON_GND_rail.COMMON_GND_rail_tap_19, Rotary_encoder_/_KY-040_heat_control.GND, Cooktop_coil_RGB_strip_+5V_/_DIN_/_GND.LED_strip_GND, Pot_temperature_indicator_strip/ring_+5V_/_DIN_/_GND.Temperature_indicator_GND, C1_1000uF_electrolytic_near_LED_power_input.-, wp_3_0_23.waypoint, wp_4_1_24.waypoint, wp_5_2_25.waypoint, wp_7_0_26.waypoint, wp_8_1_27.waypoint, wp_16_0_32.waypoint, wp_17_1_33.waypoint, wp_22_0_36.waypoint, wp_23_1_37.waypoint, wp_28_0_40.waypoint, wp_29_1_41.waypoint, wp_48_0_54.waypoint, wp_49_1_55.waypoint
  N2: Waveshare_ESP32-P4-POE-ETH_/_ESP32-P4-POE-ETH-NH.GPIO18, R2_330-470_ohm_pot_temperature_data_resistor.lead_A, wp_37_0_46.waypoint, wp_38_1_47.waypoint, wp_39_2_48.waypoint, wp_40_3_49.waypoint
  N3: Waveshare_ESP32-P4-POE-ETH_/_ESP32-P4-POE-ETH-NH.GPIO23, R1_330-470_ohm_cooktop_coil_data_resistor.lead_A, wp_31_0_42.waypoint, wp_32_1_43.waypoint
  N4: Waveshare_ESP32-P4-POE-ETH_/_ESP32-P4-POE-ETH-NH.GPIO27, Rotary_encoder_/_KY-040_heat_control.SW, wp_57_0_60.waypoint, wp_58_1_61.waypoint
  N5: Waveshare_ESP32-P4-POE-ETH_/_ESP32-P4-POE-ETH-NH.GPIO32, Rotary_encoder_/_KY-040_heat_control.A_/_CLK, wp_51_0_56.waypoint, wp_52_1_57.waypoint
  N6: Waveshare_ESP32-P4-POE-ETH_/_ESP32-P4-POE-ETH-NH.GPIO33, Rotary_encoder_/_KY-040_heat_control.B_/_DT, wp_54_0_58.waypoint, wp_55_1_59.waypoint
  N7: 5V_LED_input_from_master_power_rails.5V_LED, 5V_LED_local_rail.5V_LED_rail_tap_8, 5V_LED_local_rail.5V_LED_rail_tap_18, 5V_LED_local_rail.5V_LED_rail_tap_19, Cooktop_coil_RGB_strip_+5V_/_DIN_/_GND.LED_strip_+5V, Pot_temperature_indicator_strip/ring_+5V_/_DIN_/_GND.Temperature_indicator_+5V, C1_1000uF_electrolytic_near_LED_power_input.+, wp_0_0_21.waypoint, wp_1_1_22.waypoint, wp_13_0_30.waypoint, wp_14_1_31.waypoint, wp_19_0_34.waypoint, wp_20_1_35.waypoint, wp_25_0_38.waypoint, wp_26_1_39.waypoint
  N8: R1_330-470_ohm_cooktop_coil_data_resistor.lead_B, Cooktop_coil_RGB_strip_+5V_/_DIN_/_GND.LED_strip_DIN, wp_34_0_44.waypoint, wp_35_1_45.waypoint
  N9: R2_330-470_ohm_pot_temperature_data_resistor.lead_B, Pot_temperature_indicator_strip/ring_+5V_/_DIN_/_GND.Temperature_indicator_DIN, wp_42_0_50.waypoint, wp_43_1_51.waypoint
