# Fritzing sketch chef_station_simon_4btn_audio_editable (saved by Fritzing 1.0.7)

parts:
  DOIT_ESP32_DevKit_V1 = esp32_p30_w11 [part_number=ESP32S-PIN30]
  +12V_LED_rail = chef_simon_vplus_12v_rail
  +5V_PAM8403_rail = chef_simon_amp_5v_rail
  Common_GND_rail = chef_simon_common_ground_rail
  wp_0_0_6 = chef_simon_wire_waypoint
  wp_1_1_7 = chef_simon_wire_waypoint
  wp_2_2_8 = chef_simon_wire_waypoint
  R1_1k_gate = 1k Ω Resistor [Resistance=1k package=THT]
  R1_10k_gate_pulldown = 10k Ω Resistor [Resistance=10k package=THT]
  Q1_IRFB11N50APBF = Basic FET N-Channel [package="TO220 [THT]"]
  BTN1_4-terminal_plug = Camdenboss CTB0158-4 [part_number=CTB0158-4 package=THT]
  Ingredient_1_arcade_button_visual = Arcade Button (red)
  BTN1_local_GND_bus = chef_simon_local_ground_bus
  wp_4_0_18 = chef_simon_wire_waypoint
  wp_5_1_19 = chef_simon_wire_waypoint
  wp_6_2_20 = chef_simon_wire_waypoint
  wp_8_0_21 = chef_simon_wire_waypoint
  wp_9_1_22 = chef_simon_wire_waypoint
  wp_10_2_23 = chef_simon_wire_waypoint
  wp_12_0_24 = chef_simon_wire_waypoint
  wp_14_0_25 = chef_simon_wire_waypoint
  wp_16_0_26 = chef_simon_wire_waypoint
  wp_17_1_27 = chef_simon_wire_waypoint
  wp_18_2_28 = chef_simon_wire_waypoint
  wp_20_0_29 = chef_simon_wire_waypoint
  wp_21_1_30 = chef_simon_wire_waypoint
  wp_22_2_31 = chef_simon_wire_waypoint
  wp_24_0_32 = chef_simon_wire_waypoint
  wp_25_1_33 = chef_simon_wire_waypoint
  wp_26_2_34 = chef_simon_wire_waypoint
  wp_28_0_35 = chef_simon_wire_waypoint
  wp_29_1_36 = chef_simon_wire_waypoint
  wp_30_2_37 = chef_simon_wire_waypoint
  wp_32_0_38 = chef_simon_wire_waypoint
  wp_34_0_39 = chef_simon_wire_waypoint
  wp_36_0_40 = chef_simon_wire_waypoint
  wp_37_1_41 = chef_simon_wire_waypoint
  wp_38_2_42 = chef_simon_wire_waypoint
  wp_40_0_43 = chef_simon_wire_waypoint
  wp_41_1_44 = chef_simon_wire_waypoint
  wp_42_2_45 = chef_simon_wire_waypoint
  R2_1k_gate = 1k Ω Resistor [Resistance=1k package=THT]
  R2_10k_gate_pulldown = 10k Ω Resistor [Resistance=10k package=THT]
  Q2_IRFB11N50APBF = Basic FET N-Channel [package="TO220 [THT]"]
  BTN2_4-terminal_plug = Camdenboss CTB0158-4 [part_number=CTB0158-4 package=THT]
  Ingredient_2_arcade_button_visual = chef_simon_library_derived_green_arcade_button
  BTN2_local_GND_bus = chef_simon_local_ground_bus
  wp_44_0_55 = chef_simon_wire_waypoint
  wp_45_1_56 = chef_simon_wire_waypoint
  wp_46_2_57 = chef_simon_wire_waypoint
  wp_48_0_58 = chef_simon_wire_waypoint
  wp_49_1_59 = chef_simon_wire_waypoint
  wp_50_2_60 = chef_simon_wire_waypoint
  wp_52_0_61 = chef_simon_wire_waypoint
  wp_54_0_62 = chef_simon_wire_waypoint
  wp_56_0_63 = chef_simon_wire_waypoint
  wp_57_1_64 = chef_simon_wire_waypoint
  wp_58_2_65 = chef_simon_wire_waypoint
  wp_60_0_66 = chef_simon_wire_waypoint
  wp_61_1_67 = chef_simon_wire_waypoint
  wp_62_2_68 = chef_simon_wire_waypoint
  wp_64_0_69 = chef_simon_wire_waypoint
  wp_65_1_70 = chef_simon_wire_waypoint
  wp_66_2_71 = chef_simon_wire_waypoint
  wp_68_0_72 = chef_simon_wire_waypoint
  wp_69_1_73 = chef_simon_wire_waypoint
  wp_70_2_74 = chef_simon_wire_waypoint
  wp_72_0_75 = chef_simon_wire_waypoint
  wp_74_0_76 = chef_simon_wire_waypoint
  wp_77_1_78 = chef_simon_wire_waypoint
  wp_78_2_79 = chef_simon_wire_waypoint
  wp_80_0_80 = chef_simon_wire_waypoint
  wp_81_1_81 = chef_simon_wire_waypoint
  wp_82_2_82 = chef_simon_wire_waypoint
  R3_1k_gate = 1k Ω Resistor [Resistance=1k package=THT]
  R3_10k_gate_pulldown = 10k Ω Resistor [Resistance=10k package=THT]
  Q3_IRFB11N50APBF = Basic FET N-Channel [package="TO220 [THT]"]
  BTN3_4-terminal_plug = Camdenboss CTB0158-4 [part_number=CTB0158-4 package=THT]
  Ingredient_3_arcade_button_visual = Arcade Button (white)
  BTN3_local_GND_bus = chef_simon_local_ground_bus
  wp_84_0_92 = chef_simon_wire_waypoint
  wp_85_1_93 = chef_simon_wire_waypoint
  wp_86_2_94 = chef_simon_wire_waypoint
  wp_88_0_95 = chef_simon_wire_waypoint
  wp_89_1_96 = chef_simon_wire_waypoint
  wp_90_2_97 = chef_simon_wire_waypoint
  wp_92_0_98 = chef_simon_wire_waypoint
  wp_94_0_99 = chef_simon_wire_waypoint
  wp_96_0_100 = chef_simon_wire_waypoint
  wp_97_1_101 = chef_simon_wire_waypoint
  wp_98_2_102 = chef_simon_wire_waypoint
  wp_100_0_103 = chef_simon_wire_waypoint
  wp_101_1_104 = chef_simon_wire_waypoint
  wp_102_2_105 = chef_simon_wire_waypoint
  wp_104_0_106 = chef_simon_wire_waypoint
  wp_105_1_107 = chef_simon_wire_waypoint
  wp_106_2_108 = chef_simon_wire_waypoint
  wp_108_0_109 = chef_simon_wire_waypoint
  wp_109_1_110 = chef_simon_wire_waypoint
  wp_110_2_111 = chef_simon_wire_waypoint
  wp_112_0_112 = chef_simon_wire_waypoint
  wp_114_0_113 = chef_simon_wire_waypoint
  wp_116_0_114 = chef_simon_wire_waypoint
  wp_117_1_115 = chef_simon_wire_waypoint
  wp_118_2_116 = chef_simon_wire_waypoint
  wp_120_0_117 = chef_simon_wire_waypoint
  wp_121_1_118 = chef_simon_wire_waypoint
  wp_122_2_119 = chef_simon_wire_waypoint
  R4_1k_gate = 1k Ω Resistor [Resistance=1k package=THT]
  R4_10k_gate_pulldown = 10k Ω Resistor [Resistance=10k package=THT]
  Q4_IRFB11N50APBF = Basic FET N-Channel [package="TO220 [THT]"]
  BTN4_4-terminal_plug = Camdenboss CTB0158-4 [part_number=CTB0158-4 package=THT]
  Ingredient_4_arcade_button_visual = Arcade Button (yellow)
  BTN4_local_GND_bus = chef_simon_local_ground_bus
  wp_124_0_129 = chef_simon_wire_waypoint
  wp_125_1_130 = chef_simon_wire_waypoint
  wp_126_2_131 = chef_simon_wire_waypoint
  wp_128_0_132 = chef_simon_wire_waypoint
  wp_129_1_133 = chef_simon_wire_waypoint
  wp_130_2_134 = chef_simon_wire_waypoint
  wp_132_0_135 = chef_simon_wire_waypoint
  wp_134_0_136 = chef_simon_wire_waypoint
  wp_136_0_137 = chef_simon_wire_waypoint
  wp_137_1_138 = chef_simon_wire_waypoint
  wp_138_2_139 = chef_simon_wire_waypoint
  wp_140_0_140 = chef_simon_wire_waypoint
  wp_141_1_141 = chef_simon_wire_waypoint
  wp_142_2_142 = chef_simon_wire_waypoint
  wp_144_0_143 = chef_simon_wire_waypoint
  wp_145_1_144 = chef_simon_wire_waypoint
  wp_146_2_145 = chef_simon_wire_waypoint
  wp_148_0_146 = chef_simon_wire_waypoint
  wp_149_1_147 = chef_simon_wire_waypoint
  wp_150_2_148 = chef_simon_wire_waypoint
  wp_152_0_149 = chef_simon_wire_waypoint
  wp_154_0_150 = chef_simon_wire_waypoint
  wp_156_0_151 = chef_simon_wire_waypoint
  wp_157_1_152 = chef_simon_wire_waypoint
  wp_158_2_153 = chef_simon_wire_waypoint
  wp_160_0_154 = chef_simon_wire_waypoint
  wp_161_1_155 = chef_simon_wire_waypoint
  wp_162_2_156 = chef_simon_wire_waypoint
  Generic_PAM8403_5V_mini_amplifier = chef_simon_generic_pam8403_mini_amp [part_number=PAM8403]
  SP1_4_ohm_/_3W_speaker = SPEAKER [Resistance="4 ohm" Power=3W package=pcb_mount_speaker]
  wp_164_0_160 = chef_simon_wire_waypoint
  wp_165_1_161 = chef_simon_wire_waypoint
  wp_166_2_162 = chef_simon_wire_waypoint
  wp_168_0_163 = chef_simon_wire_waypoint
  wp_169_1_164 = chef_simon_wire_waypoint
  wp_170_2_165 = chef_simon_wire_waypoint
  wp_172_0_166 = chef_simon_wire_waypoint
  wp_173_1_167 = chef_simon_wire_waypoint
  wp_174_2_168 = chef_simon_wire_waypoint
  wp_176_0_169 = chef_simon_wire_waypoint
  wp_177_1_170 = chef_simon_wire_waypoint
  wp_178_2_171 = chef_simon_wire_waypoint
  wp_180_0_172 = chef_simon_wire_waypoint
  wp_181_1_173 = chef_simon_wire_waypoint
  wp_182_2_174 = chef_simon_wire_waypoint
  wp_184_0_175 = chef_simon_wire_waypoint
  wp_185_1_176 = chef_simon_wire_waypoint
  wp_186_2_177 = chef_simon_wire_waypoint

nets:
  N1: DOIT_ESP32_DevKit_V1.connector1, Common_GND_rail.tap0, wp_0_0_6.pin, wp_1_1_7.pin, wp_2_2_8.pin
  N2: DOIT_ESP32_DevKit_V1.connector5, BTN1_4-terminal_plug.pin3, Ingredient_1_arcade_button_visual.no_name_yet#1, wp_16_0_26.pin, wp_17_1_27.pin, wp_18_2_28.pin, wp_36_0_40.pin, wp_37_1_41.pin, wp_38_2_42.pin
  N3: DOIT_ESP32_DevKit_V1.connector6, BTN2_4-terminal_plug.pin3, wp_56_0_63.pin, wp_57_1_64.pin, wp_58_2_65.pin
  N4: DOIT_ESP32_DevKit_V1.connector8, BTN3_4-terminal_plug.pin3, Ingredient_3_arcade_button_visual.no_name_yet#1, wp_96_0_100.pin, wp_97_1_101.pin, wp_98_2_102.pin, wp_116_0_114.pin, wp_117_1_115.pin, wp_118_2_116.pin
  N5: DOIT_ESP32_DevKit_V1.connector9, BTN4_4-terminal_plug.pin3, Ingredient_4_arcade_button_visual.no_name_yet#1, wp_136_0_137.pin, wp_137_1_138.pin, wp_138_2_139.pin, wp_156_0_151.pin, wp_157_1_152.pin, wp_158_2_153.pin
  N6: DOIT_ESP32_DevKit_V1.connector10, R1_1k_gate.Pin_0, wp_20_0_29.pin, wp_21_1_30.pin, wp_22_2_31.pin
  N7: DOIT_ESP32_DevKit_V1.connector13, R2_1k_gate.Pin_0, wp_60_0_66.pin, wp_61_1_67.pin, wp_62_2_68.pin
  N8: DOIT_ESP32_DevKit_V1.connector14, R3_1k_gate.Pin_0, wp_100_0_103.pin, wp_101_1_104.pin, wp_102_2_105.pin
  N9: DOIT_ESP32_DevKit_V1.connector22, R4_1k_gate.Pin_0, wp_140_0_140.pin, wp_141_1_141.pin, wp_142_2_142.pin
  N10: DOIT_ESP32_DevKit_V1.connector23, Generic_PAM8403_5V_mini_amplifier.lin, wp_176_0_169.pin, wp_177_1_170.pin, wp_178_2_171.pin
  N11: +12V_LED_rail.tap1, BTN1_4-terminal_plug.pin1, wp_4_0_18.pin, wp_5_1_19.pin, wp_6_2_20.pin
  N12: +12V_LED_rail.tap2, BTN2_4-terminal_plug.pin1, wp_44_0_55.pin, wp_45_1_56.pin, wp_46_2_57.pin
  N13: +12V_LED_rail.tap3, BTN3_4-terminal_plug.pin1, wp_84_0_92.pin, wp_85_1_93.pin, wp_86_2_94.pin
  N14: +12V_LED_rail.tap4, BTN4_4-terminal_plug.pin1, wp_124_0_129.pin, wp_125_1_130.pin, wp_126_2_131.pin
  N15: +5V_PAM8403_rail.tap18, Generic_PAM8403_5V_mini_amplifier.vcc, wp_164_0_160.pin, wp_165_1_161.pin, wp_166_2_162.pin
  N16: Common_GND_rail.tap12, Generic_PAM8403_5V_mini_amplifier.in_gnd, wp_172_0_166.pin, wp_173_1_167.pin, wp_174_2_168.pin
  N17: Common_GND_rail.tap13, Generic_PAM8403_5V_mini_amplifier.pwr_gnd, wp_168_0_163.pin, wp_169_1_164.pin, wp_170_2_165.pin
  N18: Common_GND_rail.tap16, BTN1_local_GND_bus.tap5, wp_34_0_39.pin
  N19: Common_GND_rail.tap17, BTN2_local_GND_bus.tap5, wp_74_0_76.pin
  N20: Common_GND_rail.tap18, BTN3_local_GND_bus.tap5, wp_114_0_113.pin
  N21: Common_GND_rail.tap19, BTN4_local_GND_bus.tap5, wp_154_0_150.pin
  N22: R1_1k_gate.Pin_1, R1_10k_gate_pulldown.Pin_0, Q1_IRFB11N50APBF.gate, wp_24_0_32.pin, wp_25_1_33.pin, wp_26_2_34.pin, wp_28_0_35.pin, wp_29_1_36.pin, wp_30_2_37.pin
  N23: R1_10k_gate_pulldown.Pin_1, BTN1_local_GND_bus.tap0, wp_32_0_38.pin
  N24: Q1_IRFB11N50APBF.drain, BTN1_4-terminal_plug.pin2, wp_8_0_21.pin, wp_9_1_22.pin, wp_10_2_23.pin
  N25: Q1_IRFB11N50APBF.source, BTN1_local_GND_bus.tap1, wp_12_0_24.pin
  N26: BTN1_4-terminal_plug.pin4, Ingredient_1_arcade_button_visual.no_name_yet#2, BTN1_local_GND_bus.tap4, wp_14_0_25.pin, wp_40_0_43.pin, wp_41_1_44.pin, wp_42_2_45.pin
  N27: R2_1k_gate.Pin_1, R2_10k_gate_pulldown.Pin_0, Q2_IRFB11N50APBF.gate, wp_64_0_69.pin, wp_65_1_70.pin, wp_66_2_71.pin, wp_68_0_72.pin, wp_69_1_73.pin, wp_70_2_74.pin
  N28: R2_10k_gate_pulldown.Pin_1, BTN2_local_GND_bus.tap0, wp_72_0_75.pin
  N29: Q2_IRFB11N50APBF.drain, BTN2_4-terminal_plug.pin2, wp_48_0_58.pin, wp_49_1_59.pin, wp_50_2_60.pin
  N30: Q2_IRFB11N50APBF.source, BTN2_local_GND_bus.tap1, wp_52_0_61.pin
  N31: BTN2_4-terminal_plug.pin4, Ingredient_2_arcade_button_visual.connector2, BTN2_local_GND_bus.tap4, wp_54_0_62.pin, wp_80_0_80.pin, wp_81_1_81.pin, wp_82_2_82.pin
  N32: Ingredient_2_arcade_button_visual.connector1, wp_77_1_78.pin, wp_78_2_79.pin
  N33: R3_1k_gate.Pin_1, R3_10k_gate_pulldown.Pin_0, Q3_IRFB11N50APBF.gate, wp_104_0_106.pin, wp_105_1_107.pin, wp_106_2_108.pin, wp_108_0_109.pin, wp_109_1_110.pin, wp_110_2_111.pin
  N34: R3_10k_gate_pulldown.Pin_1, BTN3_local_GND_bus.tap0, wp_112_0_112.pin
  N35: Q3_IRFB11N50APBF.drain, BTN3_4-terminal_plug.pin2, wp_88_0_95.pin, wp_89_1_96.pin, wp_90_2_97.pin
  N36: Q3_IRFB11N50APBF.source, BTN3_local_GND_bus.tap1, wp_92_0_98.pin
  N37: BTN3_4-terminal_plug.pin4, Ingredient_3_arcade_button_visual.no_name_yet#2, BTN3_local_GND_bus.tap4, wp_94_0_99.pin, wp_120_0_117.pin, wp_121_1_118.pin, wp_122_2_119.pin
  N38: R4_1k_gate.Pin_1, R4_10k_gate_pulldown.Pin_0, Q4_IRFB11N50APBF.gate, wp_144_0_143.pin, wp_145_1_144.pin, wp_146_2_145.pin, wp_148_0_146.pin, wp_149_1_147.pin, wp_150_2_148.pin
  N39: R4_10k_gate_pulldown.Pin_1, BTN4_local_GND_bus.tap0, wp_152_0_149.pin
  N40: Q4_IRFB11N50APBF.drain, BTN4_4-terminal_plug.pin2, wp_128_0_132.pin, wp_129_1_133.pin, wp_130_2_134.pin
  N41: Q4_IRFB11N50APBF.source, BTN4_local_GND_bus.tap1, wp_132_0_135.pin
  N42: BTN4_4-terminal_plug.pin4, Ingredient_4_arcade_button_visual.no_name_yet#2, BTN4_local_GND_bus.tap4, wp_134_0_136.pin, wp_160_0_154.pin, wp_161_1_155.pin, wp_162_2_156.pin
  N43: Generic_PAM8403_5V_mini_amplifier.lminus, SP1_4_ohm_/_3W_speaker.+, wp_184_0_175.pin, wp_185_1_176.pin, wp_186_2_177.pin
  N44: Generic_PAM8403_5V_mini_amplifier.lplus, SP1_4_ohm_/_3W_speaker.-, wp_180_0_172.pin, wp_181_1_173.pin, wp_182_2_174.pin
