# Fritzing sketch chef_station_simon_orthogonal_editable (saved by Fritzing 1.0.3)

parts:
  DOIT_ESP32_DevKit_V1 = DOIT Esp32 DevKit v1 (30 pins long, 11 pins width)
  +12V_LED_rail = +12V lamp rail
  Common_GND_rail = Common ground rail
  Notes = Notes  # not connected
  ESP32_GPIOs = ESP32 GPIOs  # not connected
  R1_1k_gate = 1k Ω Resistor [Resistance=1k package=THT]
  R1_10k_gate_pulldown = 10k Ω Resistor [Resistance=10k package=THT]
  Q1_IRFB11N50APBF = Basic FET N-Channel [package="TO220 [THT]"]
  BTN1_4-terminal_plug = Camdenboss CTB0158-4 [package=THT]
  Ingredient_1_arcade_button_visual = Arcade Button (red)
  BTN1_plug_order = BTN1 plug order  # not connected
  BTN1_resistors = BTN1 resistors  # not connected
  Q1_G_/_D_/_S = Q1 G / D / S  # not connected
  wp_0_0_13 = Wire waypoint
  wp_1_1_14 = Wire waypoint
  wp_3_0_15 = Wire waypoint
  wp_4_1_16 = Wire waypoint
  wp_6_0_17 = Wire waypoint
  wp_7_1_18 = Wire waypoint
  wp_9_0_19 = Wire waypoint
  wp_10_1_20 = Wire waypoint
  wp_12_0_21 = Wire waypoint
  wp_13_1_22 = Wire waypoint
  wp_15_0_23 = Wire waypoint
  wp_16_1_24 = Wire waypoint
  wp_18_0_25 = Wire waypoint
  wp_19_1_26 = Wire waypoint
  wp_21_0_27 = Wire waypoint
  wp_22_1_28 = Wire waypoint
  wp_24_0_29 = Wire waypoint
  wp_25_1_30 = Wire waypoint
  wp_27_0_31 = Wire waypoint
  wp_28_1_32 = Wire waypoint
  wp_30_0_33 = Wire waypoint
  wp_31_1_34 = Wire waypoint
  R2_1k_gate = 1k Ω Resistor [Resistance=1k package=THT]
  R2_10k_gate_pulldown = 10k Ω Resistor [Resistance=10k package=THT]
  Q2_IRFB11N50APBF = Basic FET N-Channel [package="TO220 [THT]"]
  BTN2_4-terminal_plug = Camdenboss CTB0158-4 [package=THT]
  Ingredient_2_arcade_button_visual = Arcade Button (green, library-art derived)
  BTN2_plug_order = BTN2 plug order  # not connected
  BTN2_resistors = BTN2 resistors  # not connected
  Q2_G_/_D_/_S = Q2 G / D / S  # not connected
  wp_33_0_43 = Wire waypoint
  wp_34_1_44 = Wire waypoint
  wp_36_0_45 = Wire waypoint
  wp_37_1_46 = Wire waypoint
  wp_39_0_47 = Wire waypoint
  wp_40_1_48 = Wire waypoint
  wp_42_0_49 = Wire waypoint
  wp_43_1_50 = Wire waypoint
  wp_45_0_51 = Wire waypoint
  wp_46_1_52 = Wire waypoint
  wp_48_0_53 = Wire waypoint
  wp_49_1_54 = Wire waypoint
  wp_51_0_55 = Wire waypoint
  wp_52_1_56 = Wire waypoint
  wp_54_0_57 = Wire waypoint
  wp_55_1_58 = Wire waypoint
  wp_57_0_59 = Wire waypoint
  wp_58_1_60 = Wire waypoint
  wp_60_0_61 = Wire waypoint
  wp_61_1_62 = Wire waypoint
  wp_63_0_63 = Wire waypoint
  wp_64_1_64 = Wire waypoint
  R3_1k_gate = 1k Ω Resistor [Resistance=1k package=THT]
  R3_10k_gate_pulldown = 10k Ω Resistor [Resistance=10k package=THT]
  Q3_IRFB11N50APBF = Basic FET N-Channel [package="TO220 [THT]"]
  BTN3_4-terminal_plug = Camdenboss CTB0158-4 [package=THT]
  Ingredient_3_arcade_button_visual = Arcade Button (white)
  BTN3_plug_order = BTN3 plug order  # not connected
  BTN3_resistors = BTN3 resistors  # not connected
  Q3_G_/_D_/_S = Q3 G / D / S  # not connected
  wp_66_0_73 = Wire waypoint
  wp_67_1_74 = Wire waypoint
  wp_69_0_75 = Wire waypoint
  wp_70_1_76 = Wire waypoint
  wp_72_0_77 = Wire waypoint
  wp_73_1_78 = Wire waypoint
  wp_75_0_79 = Wire waypoint
  wp_76_1_80 = Wire waypoint
  wp_78_0_81 = Wire waypoint
  wp_79_1_82 = Wire waypoint
  wp_81_0_83 = Wire waypoint
  wp_82_1_84 = Wire waypoint
  wp_84_0_85 = Wire waypoint
  wp_85_1_86 = Wire waypoint
  wp_87_0_87 = Wire waypoint
  wp_88_1_88 = Wire waypoint
  wp_90_0_89 = Wire waypoint
  wp_91_1_90 = Wire waypoint
  wp_93_0_91 = Wire waypoint
  wp_94_1_92 = Wire waypoint
  wp_96_0_93 = Wire waypoint
  wp_97_1_94 = Wire waypoint
  R4_1k_gate = 1k Ω Resistor [Resistance=1k package=THT]
  R4_10k_gate_pulldown = 10k Ω Resistor [Resistance=10k package=THT]
  Q4_IRFB11N50APBF = Basic FET N-Channel [package="TO220 [THT]"]
  BTN4_4-terminal_plug = Camdenboss CTB0158-4 [package=THT]
  Ingredient_4_arcade_button_visual = Arcade Button (yellow)
  BTN4_plug_order = BTN4 plug order  # not connected
  BTN4_resistors = BTN4 resistors  # not connected
  Q4_G_/_D_/_S = Q4 G / D / S  # not connected
  wp_99_0_103 = Wire waypoint
  wp_100_1_104 = Wire waypoint
  wp_102_0_105 = Wire waypoint
  wp_103_1_106 = Wire waypoint
  wp_105_0_107 = Wire waypoint
  wp_106_1_108 = Wire waypoint
  wp_108_0_109 = Wire waypoint
  wp_109_1_110 = Wire waypoint
  wp_111_0_111 = Wire waypoint
  wp_112_1_112 = Wire waypoint
  wp_114_0_113 = Wire waypoint
  wp_115_1_114 = Wire waypoint
  wp_117_0_115 = Wire waypoint
  wp_118_1_116 = Wire waypoint
  wp_120_0_117 = Wire waypoint
  wp_121_1_118 = Wire waypoint
  wp_123_0_119 = Wire waypoint
  wp_124_1_120 = Wire waypoint
  wp_126_0_121 = Wire waypoint
  wp_127_1_122 = Wire waypoint
  wp_129_0_123 = Wire waypoint
  wp_130_1_124 = Wire waypoint
  R5_1k_gate = 1k Ω Resistor [Resistance=1k package=THT]
  R5_10k_gate_pulldown = 10k Ω Resistor [Resistance=10k package=THT]
  Q5_IRFB11N50APBF = Basic FET N-Channel [package="TO220 [THT]"]
  BTN5_4-terminal_plug = Camdenboss CTB0158-4 [package=THT]
  Ingredient_5_arcade_button_visual = Arcade Button (blue)
  BTN5_plug_order = BTN5 plug order  # not connected
  BTN5_resistors = BTN5 resistors  # not connected
  Q5_G_/_D_/_S = Q5 G / D / S  # not connected
  wp_132_0_133 = Wire waypoint
  wp_133_1_134 = Wire waypoint
  wp_135_0_135 = Wire waypoint
  wp_136_1_136 = Wire waypoint
  wp_138_0_137 = Wire waypoint
  wp_139_1_138 = Wire waypoint
  wp_141_0_139 = Wire waypoint
  wp_142_1_140 = Wire waypoint
  wp_144_0_141 = Wire waypoint
  wp_145_1_142 = Wire waypoint
  wp_147_0_143 = Wire waypoint
  wp_148_1_144 = Wire waypoint
  wp_150_0_145 = Wire waypoint
  wp_151_1_146 = Wire waypoint
  wp_153_0_147 = Wire waypoint
  wp_154_1_148 = Wire waypoint
  wp_156_0_149 = Wire waypoint
  wp_157_1_150 = Wire waypoint
  wp_159_0_151 = Wire waypoint
  wp_160_1_152 = Wire waypoint
  wp_162_0_153 = Wire waypoint
  wp_163_1_154 = Wire waypoint

nets:
  N1: DOIT_ESP32_DevKit_V1.RX2, BTN1_4-terminal_plug.pin3, Ingredient_1_arcade_button_visual.no_name_yet#1, wp_12_0_21.waypoint, wp_13_1_22.waypoint, wp_27_0_31.waypoint, wp_28_1_32.waypoint
  N2: DOIT_ESP32_DevKit_V1.TX2, BTN2_4-terminal_plug.pin3, Ingredient_2_arcade_button_visual.no_name_yet#1, wp_45_0_51.waypoint, wp_46_1_52.waypoint, wp_60_0_61.waypoint, wp_61_1_62.waypoint
  N3: DOIT_ESP32_DevKit_V1.D18, BTN3_4-terminal_plug.pin3, Ingredient_3_arcade_button_visual.no_name_yet#1, wp_78_0_81.waypoint, wp_79_1_82.waypoint, wp_93_0_91.waypoint, wp_94_1_92.waypoint
  N4: DOIT_ESP32_DevKit_V1.D19, BTN4_4-terminal_plug.pin3, Ingredient_4_arcade_button_visual.no_name_yet#1, wp_111_0_111.waypoint, wp_112_1_112.waypoint, wp_126_0_121.waypoint, wp_127_1_122.waypoint
  N5: DOIT_ESP32_DevKit_V1.D21, R1_1k_gate.Pin_0, wp_15_0_23.waypoint, wp_16_1_24.waypoint
  N6: DOIT_ESP32_DevKit_V1.D22, R2_1k_gate.Pin_0, wp_48_0_53.waypoint, wp_49_1_54.waypoint
  N7: DOIT_ESP32_DevKit_V1.D23, R3_1k_gate.Pin_0, wp_81_0_83.waypoint, wp_82_1_84.waypoint
  N8: DOIT_ESP32_DevKit_V1.D25, R4_1k_gate.Pin_0, wp_114_0_113.waypoint, wp_115_1_114.waypoint
  N9: DOIT_ESP32_DevKit_V1.D26, BTN5_4-terminal_plug.pin3, Ingredient_5_arcade_button_visual.no_name_yet#1, wp_144_0_141.waypoint, wp_145_1_142.waypoint, wp_159_0_151.waypoint, wp_160_1_152.waypoint
  N10: DOIT_ESP32_DevKit_V1.D27, R5_1k_gate.Pin_0, wp_147_0_143.waypoint, wp_148_1_144.waypoint
  N11: +12V_LED_rail.tap_1, +12V_LED_rail.tap_2, +12V_LED_rail.tap_3, +12V_LED_rail.tap_4, +12V_LED_rail.tap_5, BTN1_4-terminal_plug.pin1, wp_0_0_13.waypoint, wp_1_1_14.waypoint, BTN2_4-terminal_plug.pin1, wp_33_0_43.waypoint, wp_34_1_44.waypoint, BTN3_4-terminal_plug.pin1, wp_66_0_73.waypoint, wp_67_1_74.waypoint, BTN4_4-terminal_plug.pin1, wp_99_0_103.waypoint, wp_100_1_104.waypoint, BTN5_4-terminal_plug.pin1, wp_132_0_133.waypoint, wp_133_1_134.waypoint
  N12: Common_GND_rail.tap_2, Common_GND_rail.tap_3, Common_GND_rail.tap_4, Common_GND_rail.tap_5, Common_GND_rail.tap_6, Common_GND_rail.tap_7, Common_GND_rail.tap_8, Common_GND_rail.tap_9, Common_GND_rail.tap_10, Common_GND_rail.tap_11, R1_10k_gate_pulldown.Pin_1, Q1_IRFB11N50APBF.source, BTN1_4-terminal_plug.pin4, Ingredient_1_arcade_button_visual.no_name_yet#2, wp_6_0_17.waypoint, wp_7_1_18.waypoint, wp_9_0_19.waypoint, wp_10_1_20.waypoint, wp_24_0_29.waypoint, wp_25_1_30.waypoint, wp_30_0_33.waypoint, wp_31_1_34.waypoint, R2_10k_gate_pulldown.Pin_1, Q2_IRFB11N50APBF.source, BTN2_4-terminal_plug.pin4, Ingredient_2_arcade_button_visual.no_name_yet#2, wp_39_0_47.waypoint, wp_40_1_48.waypoint, wp_42_0_49.waypoint, wp_43_1_50.waypoint, wp_57_0_59.waypoint, wp_58_1_60.waypoint, wp_63_0_63.waypoint, wp_64_1_64.waypoint, R3_10k_gate_pulldown.Pin_1, Q3_IRFB11N50APBF.source, BTN3_4-terminal_plug.pin4, Ingredient_3_arcade_button_visual.no_name_yet#2, wp_72_0_77.waypoint, wp_73_1_78.waypoint, wp_75_0_79.waypoint, wp_76_1_80.waypoint, wp_90_0_89.waypoint, wp_91_1_90.waypoint, wp_96_0_93.waypoint, wp_97_1_94.waypoint, R4_10k_gate_pulldown.Pin_1, Q4_IRFB11N50APBF.source, BTN4_4-terminal_plug.pin4, Ingredient_4_arcade_button_visual.no_name_yet#2, wp_105_0_107.waypoint, wp_106_1_108.waypoint, wp_108_0_109.waypoint, wp_109_1_110.waypoint, wp_123_0_119.waypoint, wp_124_1_120.waypoint, wp_129_0_123.waypoint, wp_130_1_124.waypoint, R5_10k_gate_pulldown.Pin_1, Q5_IRFB11N50APBF.source, BTN5_4-terminal_plug.pin4, Ingredient_5_arcade_button_visual.no_name_yet#2, wp_138_0_137.waypoint, wp_139_1_138.waypoint, wp_141_0_139.waypoint, wp_142_1_140.waypoint, wp_156_0_149.waypoint, wp_157_1_150.waypoint, wp_162_0_153.waypoint, wp_163_1_154.waypoint
  N13: R1_1k_gate.Pin_1, R1_10k_gate_pulldown.Pin_0, Q1_IRFB11N50APBF.gate, wp_18_0_25.waypoint, wp_19_1_26.waypoint, wp_21_0_27.waypoint, wp_22_1_28.waypoint
  N14: Q1_IRFB11N50APBF.drain, BTN1_4-terminal_plug.pin2, wp_3_0_15.waypoint, wp_4_1_16.waypoint
  N15: R2_1k_gate.Pin_1, R2_10k_gate_pulldown.Pin_0, Q2_IRFB11N50APBF.gate, wp_51_0_55.waypoint, wp_52_1_56.waypoint, wp_54_0_57.waypoint, wp_55_1_58.waypoint
  N16: Q2_IRFB11N50APBF.drain, BTN2_4-terminal_plug.pin2, wp_36_0_45.waypoint, wp_37_1_46.waypoint
  N17: R3_1k_gate.Pin_1, R3_10k_gate_pulldown.Pin_0, Q3_IRFB11N50APBF.gate, wp_84_0_85.waypoint, wp_85_1_86.waypoint, wp_87_0_87.waypoint, wp_88_1_88.waypoint
  N18: Q3_IRFB11N50APBF.drain, BTN3_4-terminal_plug.pin2, wp_69_0_75.waypoint, wp_70_1_76.waypoint
  N19: R4_1k_gate.Pin_1, R4_10k_gate_pulldown.Pin_0, Q4_IRFB11N50APBF.gate, wp_117_0_115.waypoint, wp_118_1_116.waypoint, wp_120_0_117.waypoint, wp_121_1_118.waypoint
  N20: Q4_IRFB11N50APBF.drain, BTN4_4-terminal_plug.pin2, wp_102_0_105.waypoint, wp_103_1_106.waypoint
  N21: R5_1k_gate.Pin_1, R5_10k_gate_pulldown.Pin_0, Q5_IRFB11N50APBF.gate, wp_150_0_145.waypoint, wp_151_1_146.waypoint, wp_153_0_147.waypoint, wp_154_1_148.waypoint
  N22: Q5_IRFB11N50APBF.drain, BTN5_4-terminal_plug.pin2, wp_135_0_135.waypoint, wp_136_1_136.waypoint

custom parts:
  DOIT Esp32 DevKit v1 (30 pins long, 11 pins width): The DOIT Esp32 DevKit v1 is one of the development board created by DOIT to evaluate the ESP-WROOM-32 module. It is based on the ESP32 microcontroller that boasts Wifi, Bluetooth, Ethernet and Low Power support all in a single chip. (vanepp) made breadboard work, adjusted pin numbering and labels and reduced size of schematic and cleaned up pcb. This chip is 30pins long (2 x15) and 11 pins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
  Arcade Button (green, library-art derived): Adafruit Arcade Button (green, library-art derived)
