# Fritzing sketch chef_station_simon_native_editable (saved by Fritzing 1.0.3)

parts:
  ESP32_DevKit = ESP32 DevKit
  External_12V_lamp_supply = External 12V lamp supply
  +12V_lamp_rail = +12V lamp rail
  Common_ground_rail = Common ground rail
  Visible_wiring_notes = Visible wiring notes  # not connected
  Ingredient_1 = Ingredient 1 illuminated arcade button
  Q1_IRFB11N50APBF = IRFB11N50APBF N-channel MOSFET TO-220
  R1_100_ohm_gate = 100 ohm gate resistor
  R1_10k_pulldown = 10k gate pulldown resistor
  Ingredient_2 = Ingredient 2 illuminated arcade button
  Q2_IRFB11N50APBF = IRFB11N50APBF N-channel MOSFET TO-220
  R2_100_ohm_gate = 100 ohm gate resistor
  R2_10k_pulldown = 10k gate pulldown resistor
  Ingredient_3 = Ingredient 3 illuminated arcade button
  Q3_IRFB11N50APBF = IRFB11N50APBF N-channel MOSFET TO-220
  R3_100_ohm_gate = 100 ohm gate resistor
  R3_10k_pulldown = 10k gate pulldown resistor
  Ingredient_4 = Ingredient 4 illuminated arcade button
  Q4_IRFB11N50APBF = IRFB11N50APBF N-channel MOSFET TO-220
  R4_100_ohm_gate = 100 ohm gate resistor
  R4_10k_pulldown = 10k gate pulldown resistor
  Ingredient_5 = Ingredient 5 illuminated arcade button
  Q5_IRFB11N50APBF = IRFB11N50APBF N-channel MOSFET TO-220
  R5_100_ohm_gate = 100 ohm gate resistor
  R5_10k_pulldown = 10k gate pulldown resistor

nets:
  GND: ESP32_DevKit.GND, External_12V_lamp_supply.GND, Common_ground_rail.Tap_0, Common_ground_rail.Tap_1, Common_ground_rail.Tap_2, Common_ground_rail.Tap_3, Common_ground_rail.Tap_4, Common_ground_rail.Tap_5, Common_ground_rail.Tap_6, Common_ground_rail.Tap_7, Common_ground_rail.Tap_8, Common_ground_rail.Tap_9, Common_ground_rail.Tap_10, Common_ground_rail.Tap_11, Ingredient_1.Switch_GND, Q1_IRFB11N50APBF.Source, R1_10k_pulldown.Pin_B, Ingredient_2.Switch_GND, Q2_IRFB11N50APBF.Source, R2_10k_pulldown.Pin_B, Ingredient_3.Switch_GND, Q3_IRFB11N50APBF.Source, R3_10k_pulldown.Pin_B, Ingredient_4.Switch_GND, Q4_IRFB11N50APBF.Source, R4_10k_pulldown.Pin_B, Ingredient_5.Switch_GND, Q5_IRFB11N50APBF.Source, R5_10k_pulldown.Pin_B
  N1: ESP32_DevKit.GPIO_16_BTN1_switch, Ingredient_1.Switch_signal
  N2: ESP32_DevKit.GPIO_17_BTN2_switch, Ingredient_2.Switch_signal
  N3: ESP32_DevKit.GPIO_18_BTN3_switch, Ingredient_3.Switch_signal
  N4: ESP32_DevKit.GPIO_19_BTN4_switch, Ingredient_4.Switch_signal
  N5: ESP32_DevKit.GPIO_21_BTN1_lamp, R1_100_ohm_gate.Pin_A
  N6: ESP32_DevKit.GPIO_22_BTN2_lamp, R2_100_ohm_gate.Pin_A
  N7: ESP32_DevKit.GPIO_23_BTN3_lamp, R3_100_ohm_gate.Pin_A
  N8: ESP32_DevKit.GPIO_25_BTN4_lamp, R4_100_ohm_gate.Pin_A
  N9: ESP32_DevKit.GPIO_26_BTN5_switch, Ingredient_5.Switch_signal
  N10: ESP32_DevKit.GPIO_27_BTN5_lamp, R5_100_ohm_gate.Pin_A
  N11: External_12V_lamp_supply.+12V, +12V_lamp_rail.Tap_0, +12V_lamp_rail.Tap_1, +12V_lamp_rail.Tap_2, +12V_lamp_rail.Tap_3, +12V_lamp_rail.Tap_4, +12V_lamp_rail.Tap_5, Ingredient_1.LED_+, Ingredient_2.LED_+, Ingredient_3.LED_+, Ingredient_4.LED_+, Ingredient_5.LED_+
  N12: Ingredient_1.LED_-, Q1_IRFB11N50APBF.Drain
  N13: Q1_IRFB11N50APBF.Gate, R1_100_ohm_gate.Pin_B, R1_10k_pulldown.Pin_A
  N14: Ingredient_2.LED_-, Q2_IRFB11N50APBF.Drain
  N15: Q2_IRFB11N50APBF.Gate, R2_100_ohm_gate.Pin_B, R2_10k_pulldown.Pin_A
  N16: Ingredient_3.LED_-, Q3_IRFB11N50APBF.Drain
  N17: Q3_IRFB11N50APBF.Gate, R3_100_ohm_gate.Pin_B, R3_10k_pulldown.Pin_A
  N18: Ingredient_4.LED_-, Q4_IRFB11N50APBF.Drain
  N19: Q4_IRFB11N50APBF.Gate, R4_100_ohm_gate.Pin_B, R4_10k_pulldown.Pin_A
  N20: Ingredient_5.LED_-, Q5_IRFB11N50APBF.Drain
  N21: Q5_IRFB11N50APBF.Gate, R5_100_ohm_gate.Pin_B, R5_10k_pulldown.Pin_A
